// Logisim project CPU_Design_1.circ as structural Verilog: 5 circuits, main circuit main
module main (
  input  [15:0] Store_Data,
  input  Store,
  input  [3:0] in_3,
  input  in_4,
  output [15:0] Result,
  output [15:0] Data_Bus,
  output [15:0] out_7
);

  wire CLK_out, clock_1_out, Instruction_Decode_issinglereg, not_1_out;
  wire [2:0] Instruction_Decode_rd, Instruction_Decode_rs1, Instruction_Decode_rs2;
  wire [6:0] Instruction_Decode_short_offset;
  wire [15:0] ALU_rd, bit_extender_1_out, Register_pc_out;

  Clock clock_1 (.out(clock_1_out));
  ROM #(.addrWidth(16), .dataWidth(16)) rom_1 (.addr(Register_pc_out), .data(Data_Bus));  // open: sel
  Operation_Type_Decoder Instruction_Decode (
    .Input_Data(Data_Bus), .Short_Offset(Instruction_Decode_short_offset),
    .IsSingleReg(Instruction_Decode_issinglereg), .Rd(Instruction_Decode_rd), .Rs2(Instruction_Decode_rs2),
    .Rs1(Instruction_Decode_rs1));  // open: N, Z, S, Long_Offset
  assign bit_extender_1_out = {{9{1'b0}}, Instruction_Decode_short_offset};  // Bit_Extender bit_extender_1
  Register Register (
    .Input_Data(Result), .RegWrite(clock_1_out), .Rd(Instruction_Decode_rd), .CLK(clock_1_out),
    .Rs_2(Instruction_Decode_rs2), .Rs_1(Instruction_Decode_rs1),
    .IsSingleReg(Instruction_Decode_issinglereg), .R1(out_7), .PC_Out(Register_pc_out));  // open: Output_Data_1, Output_Data_2
  ALU ALU (
    .Rs1(Register_pc_out), .Rs2(bit_extender_1_out), .op_select(in_3), .Rd(ALU_rd));  // open: Negative_Bit, Zero_Bit
  assign Result = Store ? Store_Data : 16'bz;  // Controlled_Buffer controlled_buffer_1
  Clock CLK (.out(CLK_out));
  not not_1 (not_1_out, Store);
  RAM #(.addrWidth(16), .dataWidth(16)) ram_1 (
    .addr(ALU_rd), .data(Result), .sel(1'b1), .clk(CLK_out), .ld(not_1_out), .clr(in_4));

  // Notes on the sheet:
  //   contents of rom_1 (hex, n*v repeats v):
  //   4*2480
endmodule

module Register (
  input  RegWrite,
  input  [2:0] Rd,
  input  [2:0] Rs_2,
  input  [15:0] Input_Data,
  input  [2:0] Rs_1,
  input  IsSingleReg,
  input  CLK,
  output [15:0] Output_Data_1,
  output [15:0] Output_Data_2,
  output [15:0] R1,
  output [15:0] PC_Out
);

  wire and_1_out, and_2_out, and_3_out, and_4_out, and_5_out, and_6_out, and_7_out, decoder_1_out0,
       decoder_1_out1, decoder_1_out2, decoder_1_out3, decoder_1_out4, decoder_1_out5, decoder_1_out6,
       decoder_1_out7;
  wire [2:0] multiplexer_3_out;
  wire [15:0] adder_1_out, undriven, X0_q, X2_q, X3_q, X4_q, X5_q, X6_q;

  Decoder #(.select(3)) decoder_1 (
    .out0(decoder_1_out0), .out1(decoder_1_out1), .out2(decoder_1_out2), .out3(decoder_1_out3),
    .out4(decoder_1_out4), .out5(decoder_1_out5), .out6(decoder_1_out6), .out7(decoder_1_out7), .sel(Rd));  // open: en
  and and_1 (and_1_out, RegWrite, decoder_1_out0);
  and and_2 (and_2_out, RegWrite, decoder_1_out1);
  and and_3 (and_3_out, RegWrite, decoder_1_out2);
  and and_4 (and_4_out, RegWrite, decoder_1_out3);
  and and_5 (and_5_out, RegWrite, decoder_1_out4);
  and and_6 (and_6_out, RegWrite, decoder_1_out5);
  and and_7 (and_7_out, RegWrite, decoder_1_out6);
  Adder #(.width(16)) adder_1 (.a(16'h1), .b(PC_Out), .out(adder_1_out));  // open: cin, cout
  Register_part #(.width(16)) X0 (.D({16{1'b0}}), .Q(X0_q), .clk(and_1_out));  // open: en, clr
  Register_part #(.width(16)) X1 (.D(Input_Data), .Q(R1), .clk(and_2_out));  // open: en, clr
  Register_part #(.width(16)) X2 (.D(Input_Data), .Q(X2_q), .clk(and_3_out));  // open: en, clr
  Register_part #(.width(16)) X3 (.D(Input_Data), .Q(X3_q), .clk(and_4_out));  // open: en, clr
  Register_part #(.width(16)) X4 (.D(Input_Data), .Q(X4_q), .clk(and_5_out));  // open: en, clr
  Register_part #(.width(16)) X5 (.D(Input_Data), .Q(X5_q), .clk(and_6_out));  // open: en, clr
  Register_part #(.width(16)) X6 (.D(Input_Data), .Q(X6_q), .clk(and_7_out));  // open: en, clr
  Register_part #(.width(16)) X7 (.D(adder_1_out), .Q(PC_Out), .clk(CLK));  // open: en, clr
  Multiplexer #(.select(3), .width(16), .enable("false")) multiplexer_1 (
    .in0(X0_q), .in1(R1), .in2(X2_q), .in3(X3_q), .in4(X4_q), .in5(X5_q), .in6(X6_q), .in7(undriven),
    .out(Output_Data_1), .sel(multiplexer_3_out));
  Multiplexer #(.select(3), .width(16), .enable("false")) multiplexer_2 (
    .in0(X0_q), .in1(R1), .in2(X2_q), .in3(X3_q), .in4(X4_q), .in5(X5_q), .in6(X6_q), .in7(undriven),
    .out(Output_Data_2), .sel(Rs_2));
  Multiplexer #(.width(3), .enable("false")) multiplexer_3 (
    .in0(Rs_1), .in1(Rd), .out(multiplexer_3_out), .sel(IsSingleReg));
endmodule

module ALU (
  input  [15:0] Rs1,
  input  [15:0] Rs2,
  input  [3:0] op_select,
  output Negative_Bit,
  output Zero_Bit,
  output [15:0] Rd
);

  wire [3:0] undriven;
  wire [15:0] adder_1_out, and_1_out, divider_1_out, divider_1_rem, multiplier_1_out, nand_1_out, nor_1_out,
       not_1_out, or_1_out, shifter_1_out, shifter_2_out, shifter_3_out, shifter_4_out, shifter_5_out,
       subtractor_1_out, xor_1_out;

  Adder #(.width(16)) adder_1 (.a(Rs1), .b(Rs2), .out(adder_1_out));  // open: cin, cout
  Subtractor #(.width(16)) subtractor_1 (.a(Rs1), .b(Rs2), .out(subtractor_1_out), .bin(1'b0));  // open: bout
  Multiplier #(.width(16)) multiplier_1 (.a(Rs1), .b(Rs2), .out(multiplier_1_out));  // open: cin, cout
  Divider #(.width(16)) divider_1 (.a(Rs1), .b(Rs2), .out(divider_1_out), .rem(divider_1_rem));  // open: upper
  Shifter #(.width(16)) shifter_1 (.in(Rs1), .\dist (undriven), .out(shifter_1_out));
  Shifter #(.width(16), .shift("lr")) shifter_2 (.in(Rs1), .\dist (undriven), .out(shifter_2_out));
  Shifter #(.width(16), .shift("ar")) shifter_3 (.in(Rs1), .\dist (undriven), .out(shifter_3_out));
  Shifter #(.width(16), .shift("rl")) shifter_4 (.in(Rs1), .\dist (undriven), .out(shifter_4_out));
  Shifter #(.width(16), .shift("rr")) shifter_5 (.in(Rs1), .\dist (undriven), .out(shifter_5_out));
  assign and_1_out = Rs1 & Rs2;  // AND_Gate and_1, 16 bits wide
  assign or_1_out = Rs1 | Rs2;  // OR_Gate or_1, 16 bits wide
  assign xor_1_out = Rs1 ^ Rs2;  // XOR_Gate xor_1, 16 bits wide
  assign nand_1_out = ~(Rs1 & Rs2);  // NAND_Gate nand_1, 16 bits wide
  assign nor_1_out = ~(Rs1 | Rs2);  // NOR_Gate nor_1, 16 bits wide
  assign not_1_out = ~Rs1;  // NOT_Gate not_1, 16 bits wide
  Multiplexer #(.select(4), .width(16), .enable("false")) multiplexer_1 (
    .in0(adder_1_out), .in1(subtractor_1_out), .in2(multiplier_1_out), .in3(divider_1_out),
    .in4(divider_1_rem), .in5(and_1_out), .in6(or_1_out), .in7(xor_1_out), .in8(nand_1_out), .in9(nor_1_out),
    .in10(not_1_out), .in11(shifter_1_out), .in12(shifter_2_out), .in13(shifter_3_out), .in14(shifter_4_out),
    .in15(shifter_5_out), .out({Rd[15:1], Negative_Bit}), .sel(op_select));
  nor nor_2 (Zero_Bit, Negative_Bit, Rd[1], Rd[2], Rd[3], Rd[4], Rd[5], Rd[6], Rd[7], Rd[9], Rd[10], Rd[11], Rd[12], Rd[13], Rd[14], Rd[15], Rd[8]);

  assign Rd[0] = Negative_Bit;
endmodule

module Operation_Type_Decoder (
  input  [15:0] Input_Data,
  output [6:0] Short_Offset,
  output IsSingleReg,
  output N,
  output [2:0] Rd,
  output Z,
  output [2:0] Rs2,
  output [2:0] Rs1,
  output S,
  output [9:0] Long_Offset
);

  wire decoder_1_out9, decoder_1_out10, or_1_out;

  Multiplexer #(.width(3), .enable("false")) multiplexer_1 (
    .in0(Input_Data[8:6]), .in1(Input_Data[9:7]), .out(Rd), .sel(or_1_out));
  Decoder #(.select(4), .enable("false")) decoder_1 (
    .out9(decoder_1_out9), .out10(decoder_1_out10), .sel(Input_Data[13:10]));  // open: out0, out1, out2, out3, out4, out5, out6, out7, out8, out11, out12, out13, out14, out15
  or or_1 (or_1_out, decoder_1_out9, decoder_1_out10);

  assign IsSingleReg = 1'b1;
  assign Long_Offset = Input_Data[9:0];
  assign N = Input_Data[14];
  assign Rs1 = Input_Data[5:3];
  assign Rs2 = Input_Data[2:0];
  assign S = Input_Data[9];
  assign Short_Offset = Input_Data[6:0];
  assign Z = Input_Data[15];

  // Other names for the same wires on the sheet: Rd1[2:0] = Input_Data[8:6]; Rd2[2:0] = Input_Data[9:7];
  //   OpCode[3:0] = Input_Data[13:10]

  // Notes on the sheet:
  //   D-Type
  //   R-Type
  //   B-Type
endmodule

module Data_Seter (
  input  [3:0] Op_Type
);
endmodule
