// Logisim project CPU_Design_21.circ as structural Verilog: 5 circuits, main circuit main
module main (
  input  in_1,
  output [15:0] out_2,
  output [15:0] out_3,
  output [15:0] Result,
  output [15:0] out_5,
  output [15:0] out_6,
  output [15:0] Data_Bus,
  output [9:0] out_8
);

  wire ALUSrc, Branch, CLK, IsSingleReg, MemtoReg, MemWrite, N, not_1_out, RegWrite, S, SignExtend, Z;
  wire [2:0] Rd, Rs1, Rs2;
  wire [3:0] ALUOp, OpCode;
  wire [6:0] Short_Offset;
  wire [15:0] bit_extender_1_out, bit_extender_2_out, Extended, Long_Extended, MemAddress, PC,
       Short_Extended, WriteDatatoReg;

  Clock clock_1 (.out(CLK));
  Control Control (
    .CLK(CLK), .OpCode(OpCode), .ALUSrc(ALUSrc), .SignExtend(SignExtend), .IsSingleReg(IsSingleReg),
    .Branch(Branch), .MemWrite(MemWrite), .RegWrite(RegWrite), .MemtoReg(MemtoReg), .ALUOp(ALUOp));
  ROM #(.addrWidth(16), .dataWidth(16)) rom_1 (.addr(PC), .data(Data_Bus));  // open: sel
  Operation_Type_Decoder Instruction_Decode (
    .Input_Data(Data_Bus), .Short_Offset(Short_Offset), .OpCode(OpCode), .N(N), .Rd(Rd), .Z(Z), .Rs2(Rs2),
    .Rs1(Rs1), .S(S), .Long_Offset(out_8));
  assign bit_extender_1_out = {{9{1'b0}}, Short_Offset};  // Bit_Extender bit_extender_1
  assign bit_extender_2_out = {{6{1'b0}}, out_8};  // Bit_Extender bit_extender_2
  Multiplexer #(.width(16), .enable("false")) multiplexer_1 (
    .in0(bit_extender_1_out), .in1(bit_extender_2_out), .out(Extended), .sel(SignExtend));
  // Register Register: pin names not known; wires that end beside it: Rd, OpCode, Rs2, Rs1, IsSingleReg, PC, WriteDatatoReg, out_5, CLK, out_6, RegWrite
  assign Short_Extended = {{9{1'b0}}, Short_Offset};  // Bit_Extender bit_extender_3
  assign Long_Extended = {{6{1'b0}}, out_8};  // Bit_Extender bit_extender_4
  Multiplexer #(.width(16), .enable("false")) multiplexer_2 (.in0(out_5), .in1(Extended), .out(out_2), .sel(ALUSrc));
  assign Result = MemWrite ? out_6 : 16'bz;  // Controlled_Buffer controlled_buffer_1
  Adder #(.width(16)) adder_1 (.a(PC), .b(Extended), .out(MemAddress));  // open: cin, cout
  Multiplexer #(.width(16), .enable("false")) multiplexer_3 (
    .in0(out_3), .in1(Result), .out(WriteDatatoReg), .sel(MemtoReg));
  RAM #(.addrWidth(16), .dataWidth(16)) ram_1 (
    .addr(MemAddress), .data(Result), .sel(1'b1), .clk(CLK), .ld(not_1_out), .clr(in_1));
  not not_1 (not_1_out, MemWrite);
  ALU ALU (.Rs1(out_6), .Rs2(out_2), .op_select(ALUOp), .ALU_Result(out_3));  // open: Negative_Bit, Zero_Bit

  // Other names for the same wires on the sheet: ALU_Result[15:0] = out_3; Long_Offset[9:0] = out_8;
  //   Output_Data_1[15:0] = out_6; Output_Data_2[15:0] = out_5; Read_Data[15:0] = Result

  // Notes on the sheet:
  //   contents of rom_1 (hex, n*v repeats v):
  //   2484 2508 2883 2907 ca 919 154c 19ac 105e 1cb2 2300
  //   DType = 0
  //   BType = 1
  //   RType = 0
  //   D or B Type = 1
endmodule

module Register (
  input  RegWrite,
  input  CLK,
  input  [2:0] Rd,
  input  [2:0] Rs_2,
  input  [15:0] Input_Data,
  input  [2:0] Rs_1,
  input  IsSingleReg,
  input  [15:0] Offset,
  input  CLK_2,
  input  [3:0] OpCode,
  output [15:0] Output_Data_1,
  output [15:0] Output_Data_2,
  output [15:0] PC,
  output Branch
);

  wire ADD, ADDM, AND, and_1_out, and_2_out, and_3_out, and_4_out, and_5_out, and_6_out, and_7_out, BR,
       CLK_t, decoder_1_out0, decoder_1_out1, decoder_1_out2, decoder_1_out3, decoder_1_out4, decoder_1_out5,
       decoder_1_out6, JSR, LD, LPSW, NOT, OR, RTS, SHL, SHRA, ST, SUB, SUBM;
  wire [2:0] multiplexer_4_out;
  wire [15:0] multiplexer_1_out, X0_q, X1_q, X2_q, X3_q, X4_q, X5_q, X6_q;

  Decoder #(.select(3)) decoder_1 (
    .out0(decoder_1_out0), .out1(decoder_1_out1), .out2(decoder_1_out2), .out3(decoder_1_out3),
    .out4(decoder_1_out4), .out5(decoder_1_out5), .out6(decoder_1_out6), .sel(Rd), .en(CLK));  // open: out7
  Decoder #(.select(4), .enable("false")) decoder_2 (
    .out0(ADD), .out1(ADDM), .out2(SUB), .out3(SUBM), .out4(AND), .out5(SHL), .out6(SHRA), .out7(OR),
    .out8(NOT), .out9(LD), .out10(ST), .out11(BR), .out12(JSR), .out13(RTS), .out14(CLK_t), .out15(LPSW),
    .sel(OpCode));
  Multiplexer #(.width(16), .enable("false")) multiplexer_1 (
    .in0(16'h1), .in1(Offset), .out(multiplexer_1_out), .sel(Branch));
  and and_1 (and_1_out, RegWrite, decoder_1_out0);
  and and_2 (and_2_out, RegWrite, decoder_1_out1);
  and and_3 (and_3_out, RegWrite, decoder_1_out2);
  and and_4 (and_4_out, RegWrite, decoder_1_out3);
  and and_5 (and_5_out, RegWrite, decoder_1_out4);
  and and_6 (and_6_out, RegWrite, decoder_1_out5);
  and and_7 (and_7_out, RegWrite, decoder_1_out6);
  Adder #(.width(16)) adder_1 (.a(multiplexer_1_out), .b(PC));  // open: out, cin, cout
  Register_part #(.width(16), .trigger("high")) X0 (.D({16{1'b0}}), .Q(X0_q), .clk(and_1_out));  // open: en, clr
  Register_part #(.width(16), .trigger("high")) X1 (.D(Input_Data), .Q(X1_q), .clk(and_2_out));  // open: en, clr
  Register_part #(.width(16), .trigger("high")) X2 (.D(Input_Data), .Q(X2_q), .clk(and_3_out));  // open: en, clr
  Register_part #(.width(16), .trigger("high")) X3 (.D(Input_Data), .Q(X3_q), .clk(and_4_out));  // open: en, clr
  Register_part #(.width(16), .trigger("high")) X4 (.D(Input_Data), .Q(X4_q), .clk(and_5_out));  // open: en, clr
  Register_part #(.width(16), .trigger("high")) X5 (.D(Input_Data), .Q(X5_q), .clk(and_6_out));  // open: en, clr
  Register_part #(.width(16), .trigger("high")) X6 (.D(Input_Data), .Q(X6_q), .clk(and_7_out));  // open: en, clr
  Register_part #(.width(16), .trigger("falling")) X7 (.Q(PC), .clk(CLK_2));  // open: D, en, clr
  Multiplexer #(.select(3), .width(16), .enable("false")) multiplexer_2 (
    .in0(X0_q), .in1(X1_q), .in2(X2_q), .in3(X3_q), .in4(X4_q), .in5(X5_q), .in6(X6_q), .out(Output_Data_2),
    .sel(Rs_2));  // open: in7
  Multiplexer #(.select(3), .width(16), .enable("false")) multiplexer_3 (
    .in0(X0_q), .in1(X1_q), .in2(X2_q), .in3(X3_q), .in4(X4_q), .in5(X5_q), .in6(X6_q), .out(Output_Data_1),
    .sel(multiplexer_4_out));  // open: in7
  Multiplexer #(.width(3), .enable("false")) multiplexer_4 (
    .in0(Rs_1), .in1(Rd), .out(multiplexer_4_out), .sel(IsSingleReg));
endmodule

module ALU (
  input  [15:0] Rs1,
  input  [15:0] Rs2,
  input  [3:0] op_select,
  output Negative_Bit,
  output Zero_Bit,
  output [15:0] ALU_Result
);

  wire [15:0] adder_1_out, and_1_out, divider_1_out, divider_1_rem, multiplier_1_out, nand_1_out, nor_1_out,
       not_1_out, or_1_out, shifter_1_out, shifter_2_out, shifter_3_out, shifter_4_out, shifter_5_out,
       subtractor_1_out, xor_1_out;

  Adder #(.width(16)) adder_1 (.a(Rs1), .b(Rs2), .out(adder_1_out));  // open: cin, cout
  Subtractor #(.width(16)) subtractor_1 (.a(Rs1), .b(Rs2), .out(subtractor_1_out), .bin(1'b0));  // open: bout
  Multiplier #(.width(16)) multiplier_1 (.a(Rs1), .b(Rs2), .out(multiplier_1_out));  // open: cin, cout
  Divider #(.width(16)) divider_1 (.a(Rs1), .b(Rs2), .out(divider_1_out), .rem(divider_1_rem));  // open: upper
  Shifter #(.width(16)) shifter_1 (.in(Rs1), .\dist (Rs2[3:0]), .out(shifter_1_out));
  Shifter #(.width(16), .shift("lr")) shifter_2 (.in(Rs1), .\dist (Rs2[3:0]), .out(shifter_2_out));
  Shifter #(.width(16), .shift("ar")) shifter_3 (.in(Rs1), .\dist (Rs2[3:0]), .out(shifter_3_out));
  Shifter #(.width(16), .shift("rl")) shifter_4 (.in(Rs1), .\dist (Rs2[3:0]), .out(shifter_4_out));
  Shifter #(.width(16), .shift("rr")) shifter_5 (.in(Rs1), .\dist (Rs2[3:0]), .out(shifter_5_out));
  assign and_1_out = Rs1 & Rs2;  // AND_Gate and_1, 16 bits wide
  assign or_1_out = Rs1 | Rs2;  // OR_Gate or_1, 16 bits wide
  assign xor_1_out = Rs1 ^ Rs2;  // XOR_Gate xor_1, 16 bits wide
  assign nand_1_out = ~(Rs1 & Rs2);  // NAND_Gate nand_1, 16 bits wide
  assign nor_1_out = ~(Rs1 | Rs2);  // NOR_Gate nor_1, 16 bits wide
  assign not_1_out = ~Rs1;  // NOT_Gate not_1, 16 bits wide
  Multiplexer #(.select(4), .width(16), .enable("false")) multiplexer_1 (
    .in0(adder_1_out), .in1(subtractor_1_out), .in2(multiplier_1_out), .in3(divider_1_out),
    .in4(divider_1_rem), .in5(and_1_out), .in6(or_1_out), .in7(xor_1_out), .in8(nand_1_out), .in9(nor_1_out),
    .in10(not_1_out), .in11(shifter_1_out), .in12(shifter_2_out), .in13(shifter_3_out), .in14(shifter_4_out),
    .in15(shifter_5_out), .out(ALU_Result), .sel(op_select));
  nor nor_2 (Zero_Bit, ALU_Result[0], ALU_Result[1], ALU_Result[2], ALU_Result[3], ALU_Result[4], ALU_Result[5], ALU_Result[6], ALU_Result[7], ALU_Result[9], ALU_Result[10], ALU_Result[11], ALU_Result[12], ALU_Result[13], ALU_Result[14], ALU_Result[15], ALU_Result[8]);

  assign Negative_Bit = ALU_Result[0];
endmodule

module Operation_Type_Decoder (
  input  [15:0] Input_Data,
  output [6:0] Short_Offset,
  output [3:0] OpCode,
  output N,
  output [2:0] Rd,
  output Z,
  output [2:0] Rs2,
  output [2:0] Rs1,
  output S,
  output [9:0] Long_Offset
);

  wire ADD, ADDM, AND, BR, CLK, JSR, LD, LPSW, NOT, OR, or_1_out, RTS, SHL, SHRA, ST, SUB, SUBM;

  Decoder #(.select(4), .enable("false")) decoder_1 (
    .out0(ADD), .out1(ADDM), .out2(SUB), .out3(SUBM), .out4(AND), .out5(SHL), .out6(SHRA), .out7(OR),
    .out8(NOT), .out9(LD), .out10(ST), .out11(BR), .out12(JSR), .out13(RTS), .out14(CLK), .out15(LPSW),
    .sel(Input_Data[13:10]));
  Multiplexer #(.width(3), .enable("false")) multiplexer_1 (
    .in0(Input_Data[8:6]), .in1(Input_Data[9:7]), .out(Rd), .sel(or_1_out));
  or or_1 (or_1_out, LD, ST);

  assign Long_Offset = Input_Data[9:0];
  assign N = Input_Data[14];
  assign OpCode = Input_Data[13:10];
  assign Rs1 = Input_Data[5:3];
  assign Rs2 = Input_Data[2:0];
  assign S = Input_Data[9];
  assign Short_Offset = Input_Data[6:0];
  assign Z = Input_Data[15];

  // Other names for the same wires on the sheet: Rd1[2:0] = Input_Data[8:6]; Rd2[2:0] = Input_Data[9:7]

  // Notes on the sheet:
  //   D-Type
  //   R-Type
  //   B-Type
endmodule

module Control (
  input  CLK,
  input  [3:0] OpCode,
  output ALUSrc,
  output SignExtend,
  output IsSingleReg,
  output Branch,
  output MemWrite,
  output RegWrite,
  output MemtoReg,
  output [3:0] ALUOp
);

  wire ADD, ADDM, AND, BR, CLK_t, DType, JSR, LD, LPSW, MemtoReg0, MemtoReg1, MemtoReg2, MemtoReg3,
       MemtoReg4, MemtoReg5, MemtoReg6, MemtoReg7, MemtoReg8, MemtoReg10, MemtoReg11, MemtoReg12, MemtoReg13,
       MemtoReg14, MemtoReg15, MemWrite0, MemWrite1, MemWrite2, MemWrite3, MemWrite4, MemWrite5, MemWrite6,
       MemWrite7, MemWrite8, MemWrite9, MemWrite10, MemWrite11, MemWrite12, MemWrite13, MemWrite14,
       MemWrite15, OR, RegWrite1, RegWrite2, RegWrite3, RegWrite5, RegWrite6, RegWrite10, RegWrite11,
       RegWrite12, RegWrite13, RegWrite14, RegWrite15, RTS, RType, SUBM;

  Decoder #(.select(4), .enable("false")) decoder_1 (
    .out0(ADD), .out1(ADDM), .out2(RegWrite2), .out3(SUBM), .out4(AND), .out5(RegWrite5), .out6(RegWrite6),
    .out7(OR), .out8(MemtoReg8), .out9(LD), .out10(MemWrite10), .out11(BR), .out12(JSR), .out13(RTS),
    .out14(CLK_t), .out15(LPSW), .sel(OpCode));
  not not_1 (MemWrite0, ADD);
  not not_2 (MemtoReg0, ADD);
  not not_3 (MemWrite2, RegWrite2);
  not not_4 (MemtoReg2, RegWrite2);
  not not_5 (MemWrite9, LD);
  not not_6 (RegWrite10, MemWrite10);
  not not_7 (MemtoReg10, MemWrite10);
  or or_1 (RType, ADD, RegWrite2, AND, RegWrite5, RegWrite6, OR);
  not not_8 (MemWrite5, RegWrite5);
  not not_9 (MemtoReg5, RegWrite5);
  not not_10 (MemWrite6, RegWrite6);
  not not_11 (MemtoReg6, RegWrite6);
  not not_12 (MemWrite8, MemtoReg8);
  or or_2 (Branch, BR, JSR);
  not not_13 (ALUSrc, RType);
  not not_14 (IsSingleReg, RType);
  not not_15 (MemWrite4, AND);
  not not_16 (MemtoReg4, AND);
  not not_17 (MemWrite7, OR);
  not not_18 (MemtoReg7, OR);
  or or_3 (DType, ADDM, SUBM, MemtoReg8, LD, MemWrite10);
  Multiplexer #(.select(4)) multiplexer_1 (
    .in0(MemWrite0), .in1(MemWrite1), .in2(MemWrite2), .in3(MemWrite3), .in4(MemWrite4), .in5(MemWrite5),
    .in6(MemWrite6), .in7(MemWrite7), .in8(MemWrite8), .in9(MemWrite9), .in10(MemWrite10), .in11(MemWrite11),
    .in12(MemWrite12), .in13(MemWrite13), .in14(MemWrite14), .in15(MemWrite15), .out(MemWrite), .sel(OpCode));  // open: en
  buf or_4 (SignExtend, BR);  // OR_Gate
  Multiplexer #(.select(4)) multiplexer_2 (
    .in0(ADD), .in1(RegWrite1), .in2(RegWrite2), .in3(RegWrite3), .in4(AND), .in5(RegWrite5),
    .in6(RegWrite6), .in7(OR), .in8(MemtoReg8), .in9(LD), .in10(RegWrite10), .in11(RegWrite11),
    .in12(RegWrite12), .in13(RegWrite13), .in14(RegWrite14), .in15(RegWrite15), .out(RegWrite), .sel(OpCode));  // open: en
  Multiplexer #(.select(4)) multiplexer_3 (
    .in0(MemtoReg0), .in1(MemtoReg1), .in2(MemtoReg2), .in3(MemtoReg3), .in4(MemtoReg4), .in5(MemtoReg5),
    .in6(MemtoReg6), .in7(MemtoReg7), .in8(MemtoReg8), .in9(LD), .in10(MemtoReg10), .in11(MemtoReg11),
    .in12(MemtoReg12), .in13(MemtoReg13), .in14(MemtoReg14), .in15(MemtoReg15), .out(MemtoReg), .sel(OpCode));  // open: en
  Multiplexer #(.select(4), .width(4)) multiplexer_4 (
    .in0(4'b0000), .in1(4'b0000), .in2(4'b0001), .in3(4'b0001), .in4(4'b0101), .in5(4'b1011), .in6(4'b1100),
    .in7(4'b0110), .in8(4'b1010), .in9(4'b0000), .in10(4'b0000), .in11(4'b0000), .in12(4'b0000),
    .in13(4'b0000), .in14(4'b0000), .in15(4'b0000), .out(ALUOp), .sel(OpCode));  // open: en

  // Other names for the same wires on the sheet: BType = SignExtend; CLK_In = CLK; RegWrite0 = ADD; RegWrite4 = AND;
  //   RegWrite7 = OR; NOT = MemtoReg8; RegWrite8 = MemtoReg8; MemtoReg9 = LD; RegWrite9 = LD; SHL = RegWrite5;
  //   SHRA = RegWrite6; ST = MemWrite10; SUB = RegWrite2
endmodule
