// Logisim project 1-bit Predictor.circ as structural Verilog
module _1_bit_Predictor (
  input  Taken,
  output Prediction
);

  wire clock_1_out;

  Clock clock_1 (.out(clock_1_out));
  assign Prediction = clock_1_out ? ~Taken : 1'bz;  // Controlled_Inverter controlled_inverter_1
endmodule

module _2_bit_Predictor (
  input  Taken,
  input  Previously_Taken,
  input  PWord,
  output Prediction
);

  wire not_1_out, not_2_out;
  wire [1:0] adder_1_out, multiplexer_1_out, PWord_t, subtractor_1_out;

  not not_1 (not_1_out, Taken);
  not not_2 (not_2_out, Previously_Taken);
  // AND_Gate and_1 has open pins: in0=Taken, in4=Previously_Taken, out=open
  // AND_Gate and_2 has open pins: in0=not_1_out, in4=not_2_out, out=open
  Adder #(.width(2)) adder_1 (.a(PWord_t), .b(2'b01), .out(adder_1_out));  // open: cin, cout
  Subtractor #(.width(2)) subtractor_1 (.a(PWord_t), .b(2'b01), .out(subtractor_1_out));  // open: bin, bout
  Multiplexer #(.width(2), .enable("false")) multiplexer_1 (
    .in0(adder_1_out), .in1(subtractor_1_out), .out(multiplexer_1_out));  // open: sel
  Register #(.width(2)) register_1 (.D(multiplexer_1_out), .Q(PWord_t));  // open: en, clk, clr
endmodule
