// Logisim project Ckt_0_12.circ as structural Verilog: 14 circuits, main circuit main
module main (
  input  in_1,
  input  in_2,
  input  in_3,
  input  in_4,
  input  in_5,
  input  in_6,
  input  [1:0] in_7,
  input  in_8,
  input  [1:0] in_9,
  input  in_10,
  input  in_11,
  output [15:0] Result
);

  wire ALU_N, ALU_Z, Branch, Clock, DataHazard1, DataHazard2, IsSingleReg, JSR_Op, M_EX_MEM_OUT, M_ID_EX_OUT,
       M_Op, MemtoReg, MemWrite, N, Negative_OUT, not_1_out, PCWrite, PSW_Overwrite, RegFlush, RegWrite, S,
       Timer_Overwrite, TMP, WB_EX_MEM_OUT, WB_ID_EXOUT, WB_MEM_WB_OUT, WBSelect, Z, Zero_OUT;
  wire [1:0] Step;
  wire [2:0] Rd, Rd_EX_MEM_OUT, Rd_ID_EX_OUT, Rd_MEM_WB_OUT, Rs1, Rs2;
  wire [3:0] ALU_Op, EX_ID_EX_OUT, OpCode;
  wire [6:0] Short_Offset;
  wire [9:0] Long_Offset;
  wire [10:0] Temp1_IN, Temp1_OUT;
  wire [15:0] adder_2_out, ALU1, ALU2, ALU_Res, ALU_Res_EX_MEM_OUT, ALU_Res_IN, ALURes_OUT,
       bit_extender_1_out, bit_extender_2_out, BranchPC, Extended, Extended_ID_EX_OUT, Inst_IF_ID_OUT,
       Inst_IN, MemAddress, Output_Data_1, PC, PC_EX_MEM_IN, PC_EX_MEM_OUT, PC_ID_EX_OUT, PC_IF_ID_OUT,
       PCBranch, PCReg, Read_Data1, Read_Data1_ID_EX_OUT, Read_Data1_IN, Read_Data2, Read_Data2_EX_MEM_OUT,
       Read_Data2_ID_EX_OUT, Read_Data2_IN, ReadData_OUT, WriteBackToReg, WriteData;

  Clock clock_1 (.out(Clock));
  assign bit_extender_1_out = {{9{1'b0}}, Short_Offset};  // Bit_Extender bit_extender_1
  assign bit_extender_2_out = {{6{1'b0}}, Long_Offset};  // Bit_Extender bit_extender_2
  Multiplexer #(.width(16), .enable("false")) multiplexer_1 (
    .in0(ReadData_OUT), .out(WriteData), .sel(in_8));  // open: in1
  Multiplexer #(.width(16), .enable("false")) multiplexer_2 (
    .in0(bit_extender_1_out), .in1(bit_extender_2_out), .out(Extended), .sel(Branch));
  IF IF (.Stall(in_2), .PCWrite(PCWrite), .Branch(PCBranch), .Clock(Clock), .out_5(Inst_IN));
  Control Control_Unit (
    .ExceptionFound(in_1), .Clock(Clock), .Step(Step), .Privilaged(Clock), .OpCode(OpCode), .ALUSrc(TMP),
    .Branch(Branch), .PCV(TMP), .IsSingleReg(IsSingleReg), .M_Type(IsSingleReg), .ALUOp(ALU_Op), .M_Op(M_Op),
    .JSR_Op(JSR_Op), .Timer_Overwrite(Timer_Overwrite), .PSW_Overwrite(PSW_Overwrite), .MemWrite(MemWrite),
    .RegWrite(RegWrite), .MemtoReg(MemtoReg));
  Adder #(.width(16)) adder_1 (.a(ALU1), .b(ALU2), .out(PC_EX_MEM_IN));  // open: cin, cout
  IF_ID_Reg IF_ID (
    .Instruction_IN(Inst_IN), .PC_IN(PC), .Clock(Clock), .Enable(in_3), .Instruction_OUT(Inst_IF_ID_OUT),
    .PC_OUT(PC_IF_ID_OUT));
  Multiplexer #(.select(2), .width(16), .enable("false")) multiplexer_3 (
    .in0(Read_Data1_ID_EX_OUT), .in1(WriteBackToReg), .in2(ALU_Res_EX_MEM_OUT), .out(ALU1), .sel(in_7));  // open: in3
  Multiplexer #(.select(2), .width(16), .enable("false")) multiplexer_4 (
    .in0(Read_Data2_ID_EX_OUT), .in1(ALU_Res_EX_MEM_OUT), .in2(WriteBackToReg), .out(ALU2), .sel(in_9));  // open: in3
  HDU_2 Hazard (
    .Branch(Branch), .BrachPC(BranchPC), .RegWrite(RegWrite), .Rs1(Rs1), .Rs2(Rs2), .Rd(Rd_ID_EX_OUT),
    .BranchPC_OUT(BranchPC), .RegFlush(RegFlush), .DataHazard_1(DataHazard1), .DataHazard_2(DataHazard2));
  ID Instruction_Decoder (
    .Instruction_IN(Inst_IF_ID_OUT), .Short_Offset(Short_Offset), .OpCode(OpCode), .Rd(Rd), .N(N), .Z(Z),
    .Rs2(Rs2), .Rs1(Rs1), .S(S), .Long_Offset(Long_Offset));
  ALU ALU (
    .Rs2(Read_Data1_ID_EX_OUT), .Rs1(Read_Data2_ID_EX_OUT), .ALU_Op(EX_ID_EX_OUT), .ALU_Result(ALU_Res),
    .Zero_Bit(ALU_Z), .Negative_Bit(ALU_N));
  EX_MEM_Reg EX_MEM (
    .WB_IN(WB_ID_EXOUT), .M_IN(M_ID_EX_OUT), .PC_IN(PC_EX_MEM_IN), .Zero_IN(ALU_Z), .Negative_IN(ALU_N),
    .ALU_Res_IN(ALU_Res_IN), .ReadData2_IN(Read_Data2_ID_EX_OUT), .Rd_IN(Rd_ID_EX_OUT), .Clock(Clock),
    .Enable(in_5), .WB_OUT(WB_EX_MEM_OUT), .M_OUT(M_EX_MEM_OUT), .PC_OUT(PC_EX_MEM_OUT), .Zero_OUT(Zero_OUT),
    .Negative_OUT(Negative_OUT), .ALU_Res_OUT(ALU_Res_EX_MEM_OUT), .ReadData2_OUT(Read_Data2_EX_MEM_OUT),
    .Rd_OUT(Rd_EX_MEM_OUT));
  MEM_WB_Reg MEM_WB (
    .WB_IN(WB_EX_MEM_OUT), .ReadData_IN(Result), .ALURes_IN(ALU_Res_EX_MEM_OUT), .Rd_IN(Rd_EX_MEM_OUT),
    .Clock(Clock), .Enable(in_6), .WB_OUT(WB_MEM_WB_OUT), .ReadData_OUT(ReadData_OUT),
    .ALURes_OUT(ALURes_OUT), .Rd_OUT(Rd_MEM_WB_OUT));
  Reg Register (
    .Rs_1(Rs1), .Rd(Rd_MEM_WB_OUT), .Write_Data(WriteData), .Rs_2(Rs2), .Extended(Extended), .Clock(Clock),
    .RegWrite(WB_MEM_WB_OUT), .IsSingleReg(IsSingleReg), .OpCode(OpCode), .Read_Data1(Read_Data1),
    .Read_Data_2(Read_Data2), .PC(PCReg));
  // Probe on PC_EX_MEM_OUT
  // Probe on Extended
  assign Result = M_EX_MEM_OUT ? Output_Data_1 : 16'bz;  // Controlled_Buffer controlled_buffer_1
  // Probe on Rd
  Adder #(.width(16)) adder_2 (.a(PC_EX_MEM_OUT), .b(Extended), .out(adder_2_out));  // open: cin, cout
  not not_1 (not_1_out, M_EX_MEM_OUT);
  Multiplexer #(.width(16), .enable("false")) multiplexer_5 (
    .in0(ReadData_OUT), .in1(ALURes_OUT), .out(WriteBackToReg), .sel(WBSelect));
  ID_EX_Reg ID_EX (
    .WB_IN(RegWrite), .M_IN(MemWrite), .EX_IN(ALU_Op), .PC_IN(PC_IF_ID_OUT), .Read_Data1_IN(Read_Data1_IN),
    .Read_Data2_IN(Read_Data2_IN), .Extended_Data_IN(Extended), .Temp1_IN(Temp1_IN), .Rd_IN(Rd),
    .Clock(Clock), .Enable(in_4), .WB_OUT(WB_ID_EXOUT), .M_OUT(M_ID_EX_OUT), .EX_OUT(EX_ID_EX_OUT),
    .PC_OUT(PC_ID_EX_OUT), .Read_Data1_OUT(Read_Data1_ID_EX_OUT), .Read_Data2_Out(Read_Data2_ID_EX_OUT),
    .Extended_Data_OUT(Extended_ID_EX_OUT), .Temp1_OUT(Temp1_OUT), .Rd_OUT(Rd_ID_EX_OUT));
  // Probe on Rd_ID_EX_OUT
  Multiplexer #(.width(16), .enable("false")) multiplexer_6 (
    .in0(adder_2_out), .out(MemAddress), .sel(in_10));  // open: in1
  RAM #(.addrWidth(16), .dataWidth(16)) ram_1 (
    .addr(MemAddress), .data(Result), .sel(1'b1), .clk(Clock), .ld(not_1_out), .clr(in_11));

  // Other names for the same wires on the sheet: EX_MEM_Enable = in_5; Exception_Found = in_1; FWD1[1:0] = in_7;
  //   FWD2[1:0] = in_9; ID_EX_Enable = in_4; IF_ID_Enable = in_3; MEM_WB_Enable = in_6; Read_Data[15:0] = Result;
  //   Stall = in_2
endmodule

module Register (
  input  RegWrite,
  input  Clock,
  input  IsSingleReg,
  input  [2:0] Rs_1,
  input  [2:0] Rd,
  input  [15:0] Write_Data,
  input  [2:0] Rs_2,
  input  [3:0] OpCode,
  input  [15:0] Extended,
  output [15:0] Dead_Data1,
  output [15:0] Read_Data_2,
  output [15:0] PC
);

  wire ADD, ADDM, AND, and_1_out, and_2_out, and_3_out, and_4_out, and_5_out, and_6_out, and_7_out, BR, CLK,
       decoder_1_out0, decoder_1_out1, decoder_1_out2, decoder_1_out3, decoder_1_out4, decoder_1_out5,
       decoder_1_out6, JSR, LD, LPSW, NOT, OR, or_1_out, RTS, SHL, SHRA, ST, SUB, SUBM;
  wire [2:0] multiplexer_4_out;
  wire [15:0] adder_1_out, multiplexer_1_out, multiplexer_2_out, multiplexer_3_out, not_1_out, X0_q, X1_q,
       X2_q, X3_q, X4_q, X5_q, X6_q;

  or or_1 (or_1_out, BR, RTS, JSR);
  Decoder #(.select(3)) decoder_1 (
    .out0(decoder_1_out0), .out1(decoder_1_out1), .out2(decoder_1_out2), .out3(decoder_1_out3),
    .out4(decoder_1_out4), .out5(decoder_1_out5), .out6(decoder_1_out6), .sel(Rd), .en(Clock));  // open: out7
  assign not_1_out = ~Write_Data;  // NOT_Gate not_1, 16 bits wide
  Multiplexer #(.width(16), .enable("false")) multiplexer_1 (
    .in0(Write_Data), .in1(not_1_out), .out(multiplexer_1_out), .sel(NOT));
  Multiplexer #(.width(16), .enable("false")) multiplexer_2 (
    .in0(16'h1), .in1(Extended), .out(multiplexer_2_out), .sel(or_1_out));
  Multiplexer #(.width(16), .enable("false")) multiplexer_3 (
    .in0(PC), .in1(Dead_Data1), .out(multiplexer_3_out), .sel(RTS));
  and and_1 (and_1_out, RegWrite, decoder_1_out0);
  and and_2 (and_2_out, RegWrite, decoder_1_out1);
  and and_3 (and_3_out, RegWrite, decoder_1_out2);
  and and_4 (and_4_out, RegWrite, decoder_1_out3);
  and and_5 (and_5_out, RegWrite, decoder_1_out4);
  and and_6 (and_6_out, RegWrite, decoder_1_out5);
  and and_7 (and_7_out, RegWrite, decoder_1_out6);
  Adder #(.width(16)) adder_1 (.a(multiplexer_2_out), .b(multiplexer_3_out), .out(adder_1_out));  // open: cin, cout
  Register_part #(.width(16), .trigger("high")) X0 (.D({16{1'b0}}), .Q(X0_q), .clk(and_1_out));  // open: en, clr
  Register_part #(.width(16), .trigger("high")) X1 (.D(multiplexer_1_out), .Q(X1_q), .clk(and_2_out));  // open: en, clr
  Register_part #(.width(16), .trigger("high")) X2 (.D(multiplexer_1_out), .Q(X2_q), .clk(and_3_out));  // open: en, clr
  Register_part #(.width(16), .trigger("high")) X3 (.D(multiplexer_1_out), .Q(X3_q), .clk(and_4_out));  // open: en, clr
  Register_part #(.width(16), .trigger("high")) X4 (.D(multiplexer_1_out), .Q(X4_q), .clk(and_5_out));  // open: en, clr
  Register_part #(.width(16), .trigger("high")) X5 (.D(multiplexer_1_out), .Q(X5_q), .clk(and_6_out));  // open: en, clr
  Register_part #(.width(16), .trigger("high")) X6 (.D(multiplexer_1_out), .Q(X6_q), .clk(and_7_out));  // open: en, clr
  Register_part #(.width(16), .trigger("falling")) X7 (.D(adder_1_out), .Q(PC), .clk(Clock));  // open: en, clr
  Multiplexer #(.width(3), .enable("false")) multiplexer_4 (
    .in0(Rs_1), .in1(Rd), .out(multiplexer_4_out), .sel(IsSingleReg));
  Multiplexer #(.select(3), .width(16), .enable("false")) multiplexer_5 (
    .in0(X0_q), .in1(X1_q), .in2(X2_q), .in3(X3_q), .in4(X4_q), .in5(X5_q), .in6(X6_q), .out(Read_Data_2),
    .sel(Rs_2));  // open: in7
  Multiplexer #(.select(3), .width(16), .enable("false")) multiplexer_6 (
    .in0(X0_q), .in1(X1_q), .in2(X2_q), .in3(X3_q), .in4(X4_q), .in5(X5_q), .in6(X6_q), .out(Dead_Data1),
    .sel(multiplexer_4_out));  // open: in7
  Decoder #(.select(4), .enable("false")) decoder_2 (
    .out0(ADD), .out1(ADDM), .out2(SUB), .out3(SUBM), .out4(AND), .out5(SHL), .out6(SHRA), .out7(OR),
    .out8(NOT), .out9(LD), .out10(ST), .out11(BR), .out12(JSR), .out13(RTS), .out14(CLK), .out15(LPSW),
    .sel(OpCode));

  // Other names for the same wires on the sheet: GPR[15:0] = Dead_Data1
endmodule

module ALU (
  input  [15:0] Rs2,
  input  [15:0] Rs1,
  input  [3:0] ALU_Op,
  output [15:0] ALU_Result,
  output Zero_Bit,
  output Negative_Bit
);

  wire [15:0] adder_1_out, and_1_out, not_1_out, or_1_out, shifter_1_out, shifter_2_out, subtractor_1_out;

  Adder #(.width(16)) adder_1 (.a(Rs1), .b(Rs2), .out(adder_1_out));  // open: cin, cout
  Subtractor #(.width(16)) subtractor_1 (.a(Rs1), .b(Rs2), .out(subtractor_1_out));  // open: bin, bout
  assign and_1_out = Rs1 & Rs2;  // AND_Gate and_1, 16 bits wide
  assign or_1_out = Rs1 | Rs2;  // OR_Gate or_1, 16 bits wide
  assign not_1_out = ~Rs1;  // NOT_Gate not_1, 16 bits wide
  Shifter #(.width(16)) shifter_1 (.in(Rs1), .\dist (Rs2[3:0]), .out(shifter_1_out));
  Shifter #(.width(16), .shift("lr")) shifter_2 (.in(Rs1), .\dist (Rs2[3:0]), .out(shifter_2_out));
  Multiplexer #(.select(4), .width(16), .enable("false")) multiplexer_1 (
    .in0(adder_1_out), .in1(subtractor_1_out), .in2(and_1_out), .in3(or_1_out), .in4(not_1_out),
    .in5(shifter_1_out), .in6(shifter_2_out), .out(ALU_Result), .sel(ALU_Op));  // open: in7, in8, in9, in10, in11, in12, in13, in14, in15
  nor nor_1 (Zero_Bit, ALU_Result[0], ALU_Result[1], ALU_Result[2], ALU_Result[3], ALU_Result[4], ALU_Result[5], ALU_Result[6], ALU_Result[7], ALU_Result[9], ALU_Result[10], ALU_Result[11], ALU_Result[12], ALU_Result[13], ALU_Result[14], ALU_Result[15], ALU_Result[8]);

  assign Negative_Bit = ALU_Result[15];
endmodule

module ID (
  input  [15:0] Instruction_IN,
  output [6:0] Short_Offset,
  output [3:0] OpCode,
  output [2:0] Rd,
  output N,
  output Z,
  output [2:0] Rs2,
  output [2:0] Rs1,
  output S,
  output [9:0] Long_Offset
);

  wire ADD, ADDM, AND, BR, CLK, JSR, LD, LPSW, NOT, OR, or_1_out, RTS, SHL, SHRA, ST, SUB, SUBM;

  Decoder #(.select(4), .enable("false")) decoder_1 (
    .out0(ADD), .out1(ADDM), .out2(SUB), .out3(SUBM), .out4(AND), .out5(SHL), .out6(SHRA), .out7(OR),
    .out8(NOT), .out9(LD), .out10(ST), .out11(BR), .out12(JSR), .out13(RTS), .out14(CLK), .out15(LPSW),
    .sel(Instruction_IN[13:10]));
  Multiplexer #(.width(3), .enable("false")) multiplexer_1 (
    .in0(Instruction_IN[8:6]), .in1(Instruction_IN[9:7]), .out(Rd), .sel(or_1_out));
  or or_1 (or_1_out, JSR, LD, RTS, SUBM, ADDM, ST, NOT);

  assign Long_Offset = Instruction_IN[9:0];
  assign N = Instruction_IN[14];
  assign OpCode = Instruction_IN[13:10];
  assign Rs1 = Instruction_IN[5:3];
  assign Rs2 = Instruction_IN[2:0];
  assign S = Instruction_IN[9];
  assign Short_Offset = Instruction_IN[6:0];
  assign Z = Instruction_IN[15];

  // Other names for the same wires on the sheet: Rd1[2:0] = Instruction_IN[8:6]; Rd2[2:0] = Instruction_IN[9:7]

  // Notes on the sheet:
  //   D-Type
  //   R-Type
  //   B-Type
endmodule

module Control (
  input  ExceptionFound,
  input  Clock,
  input  [1:0] Step,
  input  Privilaged,
  input  [3:0] OpCode,
  output ALUSrc,
  output Branch,
  output PCV,
  output IsSingleReg,
  output M_Type,
  output [3:0] ALUOp,
  output M_Op,
  output JSR_Op,
  output Timer_Overwrite,
  output PSW_Overwrite,
  output MemWrite,
  output RegWrite,
  output MemtoReg
);

  wire ADD, ADDM, AND, and_2_out, BR, DType, LD, LPSW, nor_1_out, NOT, OR, or_4_out, RTS, RType, SHL, SHRA,
       ST, SUB;

  Decoder #(.select(4), .enable("false")) decoder_1 (
    .out0(ADD), .out1(ADDM), .out2(SUB), .out3(M_Op), .out4(AND), .out5(SHL), .out6(SHRA), .out7(OR),
    .out8(NOT), .out9(LD), .out10(ST), .out11(BR), .out12(JSR_Op), .out13(RTS), .out14(Timer_Overwrite),
    .out15(LPSW), .sel(OpCode));
  or or_1 (RegWrite, ADD, ADDM, SUB, M_Op, AND, SHL, SHRA, OR, NOT, LD, JSR_Op);
  or or_2 (MemtoReg, ADDM, M_Op, NOT, LD);
  // XOR_Gate xor_1 has open pins: in0=Step[0], in1=Step[1], out=open
  buf or_3 (MemWrite, ST);  // OR_Gate
  Multiplexer #(.select(4), .width(4)) multiplexer_1 (
    .in0(4'b0000), .in1(4'b0000), .in2(4'b0001), .in3(4'b0001), .in4(4'b0010), .in5(4'b0101), .in6(4'b0110),
    .in7(4'b0011), .in8(4'b0100), .in9(4'b0000), .in10(4'b0000), .in11(4'b0000), .in12(4'b0000),
    .in13(4'b0000), .in14(4'b0000), .in15(4'b0000), .out(ALUOp), .sel(OpCode));  // open: en
  or or_4 (or_4_out, Timer_Overwrite, LPSW);
  or or_5 (DType, ADDM, M_Op, NOT, LD, ST, JSR_Op, RTS);
  and and_1 (PCV, or_4_out, ~Privilaged);  // AND_Gate
  or or_6 (Branch, BR, Timer_Overwrite);
  or or_7 (RType, ADD, SUB, AND, SHL, SHRA, OR);
  nor nor_1 (nor_1_out, Step[0], Step[1]);
  and and_2 (and_2_out, ExceptionFound, nor_1_out);
  not not_1 (ALUSrc, RType);
  not not_2 (IsSingleReg, RType);
  or or_8 (M_Type, ADDM, M_Op);
  or or_9 (PSW_Overwrite, LPSW, and_2_out);

  // Other names for the same wires on the sheet: BType = Branch; CLK = Timer_Overwrite; JSR = JSR_Op; SUBM = M_Op
endmodule

module CountdownTimer (
  input  [15:0] TimerSetVal,
  input  TimerOverwrite,
  input  Clock,
  output [15:0] Timer_Output
);

  wire [15:0] multiplexer_1_out, subtractor_1_out;

  Subtractor #(.width(16)) subtractor_1 (.a(Timer_Output), .b(16'h1), .out(subtractor_1_out));  // open: bin, bout
  Register_part #(.width(16), .trigger("falling")) register_1 (
    .D(multiplexer_1_out), .Q(Timer_Output), .clk(Clock));  // open: en, clr
  Multiplexer #(.width(16), .enable("false")) multiplexer_1 (
    .in0(subtractor_1_out), .in1(TimerSetVal), .out(multiplexer_1_out), .sel(TimerOverwrite));
endmodule

module ID_EX_Reg (
  input  Clock,
  input  Enable,
  input  WB_IN,
  input  M_IN,
  input  [3:0] EX_IN,
  input  [15:0] PC_IN,
  input  [15:0] Read_Data1_IN,
  input  [15:0] Read_Data2_IN,
  input  [15:0] Extended_Data_IN,
  input  [10:0] Temp1_IN,
  input  [2:0] Rd_IN,
  output WB_OUT,
  output M_OUT,
  output [3:0] EX_OUT,
  output [15:0] PC_OUT,
  output [15:0] Read_Data1_OUT,
  output [15:0] Read_Data2_Out,
  output [15:0] Extended_Data_OUT,
  output [10:0] Temp1_OUT,
  output [2:0] Rd_OUT
);

  wire register_1_q, register_2_q;
  wire [2:0] register_14_q;
  wire [3:0] register_3_q;
  wire [10:0] register_13_q;
  wire [15:0] register_4_q, register_5_q, register_11_q, register_12_q;

  Register_part #(.width(1), .trigger("falling")) register_1 (
    .D(WB_IN), .en(Enable), .Q(register_1_q), .clk(Clock));  // open: clr
  Register_part #(.width(1), .trigger("falling")) register_2 (
    .D(M_IN), .en(Enable), .Q(register_2_q), .clk(Clock));  // open: clr
  Register_part #(.width(4), .trigger("falling")) register_3 (
    .D(EX_IN), .en(Enable), .Q(register_3_q), .clk(Clock));  // open: clr
  Register_part #(.width(16), .trigger("falling")) register_4 (
    .D(PC_IN), .en(Enable), .Q(register_4_q), .clk(Clock));  // open: clr
  Register_part #(.width(16), .trigger("falling")) register_5 (
    .D(Read_Data1_IN), .en(Enable), .Q(register_5_q), .clk(Clock));  // open: clr
  Register_part #(.width(1)) register_6 (.D(register_1_q), .en(Enable), .Q(WB_OUT), .clk(Clock));  // open: clr
  Register_part #(.width(1)) register_7 (.D(register_2_q), .en(Enable), .Q(M_OUT), .clk(Clock));  // open: clr
  Register_part #(.width(4)) register_8 (.D(register_3_q), .en(Enable), .Q(EX_OUT), .clk(Clock));  // open: clr
  Register_part #(.width(16)) register_9 (.D(register_4_q), .en(Enable), .Q(PC_OUT), .clk(Clock));  // open: clr
  Register_part #(.width(16)) register_10 (
    .D(register_5_q), .en(Enable), .Q(Read_Data1_OUT), .clk(Clock));  // open: clr
  Register_part #(.width(16), .trigger("falling")) register_11 (
    .D(Read_Data2_IN), .en(Enable), .Q(register_11_q), .clk(Clock));  // open: clr
  Register_part #(.width(16), .trigger("falling")) register_12 (
    .D(Extended_Data_IN), .en(Enable), .Q(register_12_q), .clk(Clock));  // open: clr
  Register_part #(.width(11), .trigger("falling")) register_13 (
    .D(Temp1_IN), .en(Enable), .Q(register_13_q), .clk(Clock));  // open: clr
  Register_part #(.width(3), .trigger("falling")) register_14 (
    .D(Rd_IN), .en(Enable), .Q(register_14_q), .clk(Clock));  // open: clr
  Register_part #(.width(16)) register_15 (
    .D(register_11_q), .en(Enable), .Q(Read_Data2_Out), .clk(Clock));  // open: clr
  Register_part #(.width(16)) register_16 (
    .D(register_12_q), .en(Enable), .Q(Extended_Data_OUT), .clk(Clock));  // open: clr
  Register_part #(.width(11)) register_17 (.D(register_13_q), .en(Enable), .Q(Temp1_OUT), .clk(Clock));  // open: clr
  Register_part #(.width(3)) register_18 (.D(register_14_q), .en(Enable), .Q(Rd_OUT), .clk(Clock));  // open: clr

  // Other names for the same wires on the sheet: Extended_Data1_IN[15:0] = Extended_Data_IN;
  //   Extended_Data1_OUT[15:0] = Extended_Data_OUT
endmodule

module EX_MEM_Reg (
  input  Clock,
  input  Enable,
  input  WB_IN,
  input  M_IN,
  input  [15:0] PC_IN,
  input  Zero_IN,
  input  Negative_IN,
  input  [15:0] ALU_Res_IN,
  input  [15:0] ReadData2_IN,
  input  [2:0] Rd_IN,
  output WB_OUT,
  output M_OUT,
  output [15:0] PC_OUT,
  output Zero_OUT,
  output Negative_OUT,
  output [15:0] ALU_Res_OUT,
  output [15:0] ReadData2_OUT,
  output [2:0] Rd_OUT
);

  wire register_1_q, register_2_q, register_4_q, register_5_q;
  wire [2:0] register_13_q;
  wire [15:0] register_3_q, register_11_q, register_12_q;

  Register_part #(.width(1), .trigger("falling")) register_1 (
    .D(WB_IN), .en(Enable), .Q(register_1_q), .clk(Clock));  // open: clr
  Register_part #(.width(1), .trigger("falling")) register_2 (
    .D(M_IN), .en(Enable), .Q(register_2_q), .clk(Clock));  // open: clr
  Register_part #(.width(16), .trigger("falling")) register_3 (
    .D(PC_IN), .en(Enable), .Q(register_3_q), .clk(Clock));  // open: clr
  Register_part #(.width(1), .trigger("falling")) register_4 (
    .D(Zero_IN), .en(Enable), .Q(register_4_q), .clk(Clock));  // open: clr
  Register_part #(.width(1), .trigger("falling")) register_5 (
    .D(Negative_IN), .en(Enable), .Q(register_5_q), .clk(Clock));  // open: clr
  Register_part #(.width(1)) register_6 (.D(register_1_q), .en(Enable), .Q(WB_OUT), .clk(Clock));  // open: clr
  Register_part #(.width(1)) register_7 (.D(register_2_q), .en(Enable), .Q(M_OUT), .clk(Clock));  // open: clr
  Register_part #(.width(16)) register_8 (.D(register_3_q), .en(Enable), .Q(PC_OUT), .clk(Clock));  // open: clr
  Register_part #(.width(1)) register_9 (.D(register_4_q), .en(Enable), .Q(Zero_OUT), .clk(Clock));  // open: clr
  Register_part #(.width(1)) register_10 (.D(register_5_q), .en(Enable), .Q(Negative_OUT), .clk(Clock));  // open: clr
  Register_part #(.width(16), .trigger("falling")) register_11 (
    .D(ALU_Res_IN), .en(Enable), .Q(register_11_q), .clk(Clock));  // open: clr
  Register_part #(.width(16), .trigger("falling")) register_12 (
    .D(ReadData2_IN), .en(Enable), .Q(register_12_q), .clk(Clock));  // open: clr
  Register_part #(.width(3), .trigger("falling")) register_13 (
    .D(Rd_IN), .en(Enable), .Q(register_13_q), .clk(Clock));  // open: clr
  Register_part #(.width(16)) register_14 (.D(register_11_q), .en(Enable), .Q(ALU_Res_OUT), .clk(Clock));  // open: clr
  Register_part #(.width(16)) register_15 (
    .D(register_12_q), .en(Enable), .Q(ReadData2_OUT), .clk(Clock));  // open: clr
  Register_part #(.width(3)) register_16 (.D(register_13_q), .en(Enable), .Q(Rd_OUT), .clk(Clock));  // open: clr
endmodule

module MEM_WB_Reg (
  input  Clock,
  input  Enable,
  input  WB_IN,
  input  [15:0] ReadData_IN,
  input  [15:0] ALURes_IN,
  input  [2:0] Rd_IN,
  output WB_OUT,
  output [15:0] ReadData_OUT,
  output [15:0] ALURes_OUT,
  output [2:0] Rd_OUT
);

  wire register_1_q;
  wire [2:0] register_4_q;
  wire [15:0] register_2_q, register_3_q;

  Register_part #(.width(1), .trigger("falling")) register_1 (
    .D(WB_IN), .en(Enable), .Q(register_1_q), .clk(Clock));  // open: clr
  Register_part #(.width(16), .trigger("falling")) register_2 (
    .D(ReadData_IN), .en(Enable), .Q(register_2_q), .clk(Clock));  // open: clr
  Register_part #(.width(16), .trigger("falling")) register_3 (
    .D(ALURes_IN), .en(Enable), .Q(register_3_q), .clk(Clock));  // open: clr
  Register_part #(.width(3), .trigger("falling")) register_4 (
    .D(Rd_IN), .en(Enable), .Q(register_4_q), .clk(Clock));  // open: clr
  Register_part #(.width(1)) register_5 (.D(register_1_q), .en(Enable), .Q(WB_OUT), .clk(Clock));  // open: clr
  Register_part #(.width(16)) register_6 (.D(register_2_q), .en(Enable), .Q(ReadData_OUT), .clk(Clock));  // open: clr
  Register_part #(.width(16)) register_7 (.D(register_3_q), .en(Enable), .Q(ALURes_OUT), .clk(Clock));  // open: clr
  Register_part #(.width(3)) register_8 (.D(register_4_q), .en(Enable), .Q(Rd_OUT), .clk(Clock));  // open: clr
endmodule

module IF_ID_Reg (
  input  Clock,
  input  Enable,
  input  [15:0] Instruction_IN,
  input  [15:0] PC_IN,
  output [15:0] Instruction_OUT,
  output [15:0] PC_OUT
);

  wire [15:0] register_1_q, register_2_q;

  Register_part #(.width(16), .trigger("falling")) register_1 (
    .D(Instruction_IN), .en(Enable), .Q(register_1_q), .clk(Clock));  // open: clr
  Register_part #(.width(16), .trigger("falling")) register_2 (
    .D(PC_IN), .en(Enable), .Q(register_2_q), .clk(Clock));  // open: clr
  Register_part #(.width(16)) register_3 (
    .D(register_1_q), .en(Enable), .Q(Instruction_OUT), .clk(Clock));  // open: clr
  Register_part #(.width(16)) register_4 (.D(register_2_q), .en(Enable), .Q(PC_OUT), .clk(Clock));  // open: clr
endmodule

module Hazard_Detection_Unit (
  input  [2:0] RD_IN,
  input  M_IN,
  input  Brach,
  input  ID_EX_RS,
  input  RegWrite,
  input  [2:0] Rs1,
  input  [2:0] Rs2,
  input  [2:0] Rd,
  output PC_OUT,
  output RegFlush,
  output Stall
);

  wire comparator_1_eq, comparator_2_eq, or_1_out;

  Comparator #(.width(3)) comparator_1 (.a(Rs1), .b(Rd), .eq(comparator_1_eq));  // open: gt, lt
  Comparator #(.width(3)) comparator_2 (.a(Rs2), .b(Rd), .eq(comparator_2_eq));  // open: gt, lt
  or or_1 (or_1_out, comparator_1_eq, comparator_2_eq);
  and and_1 (Stall, or_1_out, RegWrite);

  assign RegFlush = Brach;

  // Other names for the same wires on the sheet: Branch = Brach
endmodule

module Reg (
  input  RegWrite,
  input  Clock,
  input  IsSingleReg,
  input  [2:0] Rs_1,
  input  [2:0] Rd,
  input  [15:0] Write_Data,
  input  [2:0] Rs_2,
  input  [3:0] OpCode,
  input  [15:0] Extended,
  output [15:0] Read_Data1,
  output [15:0] Read_Data_2,
  output [15:0] PC
);

  wire ADD, ADDM, AND, and_1_out, and_2_out, and_3_out, and_4_out, and_5_out, and_6_out, and_7_out, BR, CLK,
       decoder_1_out0, decoder_1_out1, decoder_1_out2, decoder_1_out3, decoder_1_out4, decoder_1_out5,
       decoder_1_out6, JSR, LD, LPSW, NOT, OR, or_1_out, RTS, SHL, SHRA, ST, SUB, SUBM;
  wire [2:0] multiplexer_4_out;
  wire [15:0] adder_1_out, multiplexer_1_out, multiplexer_2_out, multiplexer_3_out, not_1_out, X0_q, X1_q,
       X2_q, X3_q, X4_q, X5_q, X6_q;

  or or_1 (or_1_out, BR, RTS, JSR);
  Decoder #(.select(3)) decoder_1 (
    .out0(decoder_1_out0), .out1(decoder_1_out1), .out2(decoder_1_out2), .out3(decoder_1_out3),
    .out4(decoder_1_out4), .out5(decoder_1_out5), .out6(decoder_1_out6), .sel(Rd), .en(Clock));  // open: out7
  assign not_1_out = ~Write_Data;  // NOT_Gate not_1, 16 bits wide
  Multiplexer #(.width(16), .enable("false")) multiplexer_1 (
    .in0(Write_Data), .in1(not_1_out), .out(multiplexer_1_out), .sel(NOT));
  Multiplexer #(.width(16), .enable("false")) multiplexer_2 (
    .in0(16'h1), .in1(Extended), .out(multiplexer_2_out), .sel(or_1_out));
  Multiplexer #(.width(16), .enable("false")) multiplexer_3 (
    .in0(PC), .in1(Read_Data1), .out(multiplexer_3_out), .sel(RTS));
  and and_1 (and_1_out, RegWrite, decoder_1_out0);
  and and_2 (and_2_out, RegWrite, decoder_1_out1);
  and and_3 (and_3_out, RegWrite, decoder_1_out2);
  and and_4 (and_4_out, RegWrite, decoder_1_out3);
  and and_5 (and_5_out, RegWrite, decoder_1_out4);
  and and_6 (and_6_out, RegWrite, decoder_1_out5);
  and and_7 (and_7_out, RegWrite, decoder_1_out6);
  Adder #(.width(16)) adder_1 (.a(multiplexer_2_out), .b(multiplexer_3_out), .out(adder_1_out));  // open: cin, cout
  Register_part #(.width(16), .trigger("high")) X0 (.D({16{1'b0}}), .Q(X0_q), .clk(and_1_out));  // open: en, clr
  Register_part #(.width(16), .trigger("high")) X1 (.D(multiplexer_1_out), .Q(X1_q), .clk(and_2_out));  // open: en, clr
  Register_part #(.width(16), .trigger("high")) X2 (.D(multiplexer_1_out), .Q(X2_q), .clk(and_3_out));  // open: en, clr
  Register_part #(.width(16), .trigger("high")) X3 (.D(multiplexer_1_out), .Q(X3_q), .clk(and_4_out));  // open: en, clr
  Register_part #(.width(16), .trigger("high")) X4 (.D(multiplexer_1_out), .Q(X4_q), .clk(and_5_out));  // open: en, clr
  Register_part #(.width(16), .trigger("high")) X5 (.D(multiplexer_1_out), .Q(X5_q), .clk(and_6_out));  // open: en, clr
  Register_part #(.width(16), .trigger("high")) X6 (.D(multiplexer_1_out), .Q(X6_q), .clk(and_7_out));  // open: en, clr
  Register_part #(.width(16), .trigger("falling")) X7 (.D(adder_1_out), .Q(PC), .clk(Clock));  // open: en, clr
  Multiplexer #(.width(3), .enable("false")) multiplexer_4 (
    .in0(Rs_1), .in1(Rd), .out(multiplexer_4_out), .sel(IsSingleReg));
  Multiplexer #(.select(3), .width(16), .enable("false")) multiplexer_5 (
    .in0(X0_q), .in1(X1_q), .in2(X2_q), .in3(X3_q), .in4(X4_q), .in5(X5_q), .in6(X6_q), .out(Read_Data_2),
    .sel(Rs_2));  // open: in7
  Multiplexer #(.select(3), .width(16), .enable("false")) multiplexer_6 (
    .in0(X0_q), .in1(X1_q), .in2(X2_q), .in3(X3_q), .in4(X4_q), .in5(X5_q), .in6(X6_q), .out(Read_Data1),
    .sel(multiplexer_4_out));  // open: in7
  Decoder #(.select(4), .enable("false")) decoder_2 (
    .out0(ADD), .out1(ADDM), .out2(SUB), .out3(SUBM), .out4(AND), .out5(SHL), .out6(SHRA), .out7(OR),
    .out8(NOT), .out9(LD), .out10(ST), .out11(BR), .out12(JSR), .out13(RTS), .out14(CLK), .out15(LPSW),
    .sel(OpCode));

  // Other names for the same wires on the sheet: GPR[15:0] = Read_Data1
endmodule

module IF (
  input  Clock,
  input  Stall,
  input  PCWrite,
  input  [15:0] Branch,
  output [15:0] out_5
);

  wire [15:0] adder_1_out, multiplexer_1_out, multiplexer_2_out, multiplexer_3_out, PC;

  Multiplexer #(.width(16), .enable("false")) multiplexer_1 (
    .in0(PC), .in1(Branch), .out(multiplexer_1_out), .sel(PCWrite));
  Multiplexer #(.width(16), .enable("false")) multiplexer_2 (
    .in0(16'h1), .in1({16{1'b0}}), .out(multiplexer_2_out), .sel(PCWrite));
  Adder #(.width(16)) adder_1 (.a(multiplexer_1_out), .b(multiplexer_2_out), .out(adder_1_out));  // open: cin, cout
  Multiplexer #(.width(16), .enable("false")) multiplexer_3 (
    .in0(adder_1_out), .in1(PC), .out(multiplexer_3_out), .sel(Stall));
  Register_part #(.width(16), .trigger("falling")) u_PC (.D(multiplexer_3_out), .Q(PC), .clk(Clock));  // open: en, clr
  ROM #(.addrWidth(16), .dataWidth(16)) rom_1 (.addr(PC), .data(out_5));  // open: sel

  // Other names for the same wires on the sheet: Inst_IN[15:0] = out_5

  // Notes on the sheet:
  //   contents of rom_1 (hex, n*v repeats v):
  //   2484 2508 2883 2907 ca
endmodule

module HDU_2 (
  input  Branch,
  input  [15:0] BrachPC,
  input  RegWrite,
  input  [2:0] Rs1,
  input  [2:0] Rs2,
  input  [2:0] Rd,
  output [15:0] BranchPC_OUT,
  output RegFlush,
  output DataHazard_1,
  output DataHazard_2
);

  wire comparator_1_eq, comparator_2_eq;

  Comparator #(.width(3)) comparator_1 (.a(Rs1), .b(Rd), .eq(comparator_1_eq));  // open: gt, lt
  Comparator #(.width(3)) comparator_2 (.a(Rs2), .b(Rd), .eq(comparator_2_eq));  // open: gt, lt
  and and_1 (DataHazard_1, comparator_1_eq, RegWrite);
  and and_2 (DataHazard_2, comparator_2_eq, RegWrite);

  assign BranchPC_OUT = BrachPC;
  assign RegFlush = Branch;

  // Other names for the same wires on the sheet: BranchPC[15:0] = BrachPC
endmodule
