// Logisim project Ckt_0_7.circ as structural Verilog: 11 circuits, main circuit main
module main (
  input  in_1,
  output [15:0] Result
);

  wire ALU_N, ALU_Z, Clock, EX_IN, EX_OUT, EXMEM_RegWrite, IsSingleReg, M_IN, M_OUT, N, Negative_IN,
       Negative_OUT, not_1_out, RegWrite, S, WB_IN, WB_OUT, Z, Zero_IN, Zero_OUT;
  wire [2:0] Rd, Rs1, Rs2;
  wire [3:0] ALU_OpCode, OpCode, OpCode_IN, OpCode_OUT;
  wire [6:0] Short_Offset;
  wire [9:0] Long_Offset;
  wire [15:0] adder_1_out, ALU_Res, ALU_Res_IN, ALU_Res_OUT, ALURes_IN, ALURes_OUT, Extended,
       Extended_Data1_IN, Extended_Data1_OUT, Inst_IF_ID_IN, Inst_IF_ID_OUT, Inst_IN, MemAddress,
       Output_Data_1, PC, PC_IF_ID_IN, PC_IF_ID_OUT, PC_IN, PC_OUT, PCReg, Read_Data1, Read_Data1_IN,
       Read_Data1_OUT, Read_Data2, Read_Data2_IN, Read_Data2_OUT, ReadData_IN, ReadData_OUT, Temp1_IN,
       Temp1_OUT, WriteDataReg;

  Clock clock_1 (.out(Clock));
  Control Control_Unit (.Clock(Clock));  // open: ExceptionFound, Step, Privilaged, OpCode, ALUSrc, Branch, PCV, IsSingleReg, M_Type, ALUOp, M_Op, JSR_Op, Timer_Overwrite, PSW_Overwrite, Stage_1, Stage_2, Stage_3, Stage_4, MemWrite, RegWrite, MemtoReg
  Register_part #(.width(16), .trigger("falling")) u_PC (.D(adder_1_out), .Q(PC), .clk(Clock));  // open: en, clr
  Adder #(.width(16)) adder_1 (.a(PC), .b(16'h1), .out(adder_1_out));  // open: cin, cout
  ROM #(.addrWidth(16), .dataWidth(16)) rom_1 (.addr(PC), .data(Inst_IN));  // open: sel
  IF_ID_Reg IF_ID (
    .Instruction_IN(Inst_IF_ID_IN), .PC_IN(PC_IF_ID_IN), .Clock(Clock), .Enable(1'b1),
    .Instruction_OUT(Inst_IF_ID_OUT), .PC_OUT(PC_IF_ID_OUT));
  ID Instruction_Decoder (
    .Instruction_IN(Inst_IF_ID_OUT), .Short_Offset(Short_Offset), .OpCode(OpCode), .Rd(Rd), .N(N), .Z(Z),
    .Rs2(Rs2), .Rs1(Rs1), .S(S), .Long_Offset(Long_Offset));
  Reg Register (
    .Rs_1(Rs1), .Rd(Rd), .Write_Data(WriteDataReg), .Rs_2(Rs2), .Extended(Extended), .Clock(Clock),
    .RegWrite(RegWrite), .IsSingleReg(IsSingleReg), .OpCode(OpCode), .Read_Data1(Read_Data1),
    .Read_Data_2(Read_Data2), .PC(PCReg));
  ID_EX_Reg ID_EX (
    .WB_IN(WB_IN), .M_IN(M_IN), .EX_IN(EX_IN), .PC_IN(PC_IN), .Read_Data1_IN(Read_Data1_IN),
    .Read_Data2_IN(Read_Data2_IN), .Extended_Data_IN(Extended_Data1_IN), .Temp1_IN(Temp1_IN[10:0]),
    .OpCode_IN(OpCode_IN), .Clock(Clock), .Enable(1'b1), .WB_OUT(WB_OUT), .M_OUT(M_OUT), .EX_OUT(EX_OUT),
    .PC_OUT(PC_OUT), .Read_Data1_OUT(Read_Data1_OUT), .Read_Data2_Out(Read_Data2_OUT),
    .Extended_Data_OUT(Extended_Data1_OUT), .Temp1_OUT(Temp1_OUT[10:0]), .OpCode_OUT(OpCode_OUT));
  ALU ALU (
    .Rs2(Read_Data2), .Rs1(Read_Data1), .ALU_Op(ALU_OpCode), .ALU_Result(ALU_Res), .Zero_Bit(ALU_Z),
    .Negative_Bit(ALU_N));
  EX_MEM_Reg EX_MEM (
    .WB_IN(WB_IN), .M_IN(M_IN), .PC_IN(PC_IN), .Zero_IN(Zero_IN), .Negative_IN(Negative_IN),
    .ALU_Res_IN(ALU_Res_IN), .Temp1_IN(Temp1_IN), .Clock(Clock), .Enable(1'b1), .WB_OUT(WB_OUT),
    .M_OUT(M_OUT), .PC_OUT(PC_OUT), .Zero_OUT(Zero_OUT), .Negative_OUT(Negative_OUT),
    .ALU_Res_OUT(ALU_Res_OUT), .Temp1_OUT(Temp1_OUT));
  assign Result = EXMEM_RegWrite ? Output_Data_1 : 16'bz;  // Controlled_Buffer controlled_buffer_1
  not not_1 (not_1_out, EXMEM_RegWrite);
  RAM #(.addrWidth(16), .dataWidth(16)) ram_1 (
    .addr(MemAddress), .data(Result), .sel(1'b1), .clk(Clock), .ld(not_1_out), .clr(in_1));
  MEM_WB_Reg mem_wb_reg_1 (
    .WB_IN(WB_IN), .ReadData_IN(ReadData_IN), .ALURes_IN(ALURes_IN), .Clock(Clock), .Enable(1'b1),
    .WB_OUT(WB_OUT), .ReadData_OUT(ReadData_OUT), .ALURes_OUT(ALURes_OUT));
  // Pins of 11 and 16 bits meet at Temp1_IN
  // Pins of 11 and 16 bits meet at Temp1_OUT

  // Other names for the same wires on the sheet: Read_Data[15:0] = Result

  // Notes on the sheet:
  //   contents of rom_1 (hex, n*v repeats v):
  //   2484 2508 2883 2907 ca
endmodule

module Register (
  input  RegWrite,
  input  Clock,
  input  IsSingleReg,
  input  [2:0] Rs_1,
  input  [2:0] Rd,
  input  [15:0] Write_Data,
  input  [2:0] Rs_2,
  input  [3:0] OpCode,
  input  [15:0] Extended,
  output [15:0] Dead_Data1,
  output [15:0] Read_Data_2,
  output [15:0] PC
);

  wire ADD, ADDM, AND, and_1_out, and_2_out, and_3_out, and_4_out, and_5_out, and_6_out, and_7_out, BR, CLK,
       decoder_1_out0, decoder_1_out1, decoder_1_out2, decoder_1_out3, decoder_1_out4, decoder_1_out5,
       decoder_1_out6, JSR, LD, LPSW, NOT, OR, or_1_out, RTS, SHL, SHRA, ST, SUB, SUBM;
  wire [2:0] multiplexer_4_out;
  wire [15:0] adder_1_out, multiplexer_1_out, multiplexer_2_out, multiplexer_3_out, not_1_out, X0_q, X1_q,
       X2_q, X3_q, X4_q, X5_q, X6_q;

  or or_1 (or_1_out, BR, RTS, JSR);
  Decoder #(.select(3)) decoder_1 (
    .out0(decoder_1_out0), .out1(decoder_1_out1), .out2(decoder_1_out2), .out3(decoder_1_out3),
    .out4(decoder_1_out4), .out5(decoder_1_out5), .out6(decoder_1_out6), .sel(Rd), .en(Clock));  // open: out7
  assign not_1_out = ~Write_Data;  // NOT_Gate not_1, 16 bits wide
  Multiplexer #(.width(16), .enable("false")) multiplexer_1 (
    .in0(Write_Data), .in1(not_1_out), .out(multiplexer_1_out), .sel(NOT));
  Multiplexer #(.width(16), .enable("false")) multiplexer_2 (
    .in0(16'h1), .in1(Extended), .out(multiplexer_2_out), .sel(or_1_out));
  Multiplexer #(.width(16), .enable("false")) multiplexer_3 (
    .in0(PC), .in1(Dead_Data1), .out(multiplexer_3_out), .sel(RTS));
  and and_1 (and_1_out, RegWrite, decoder_1_out0);
  and and_2 (and_2_out, RegWrite, decoder_1_out1);
  and and_3 (and_3_out, RegWrite, decoder_1_out2);
  and and_4 (and_4_out, RegWrite, decoder_1_out3);
  and and_5 (and_5_out, RegWrite, decoder_1_out4);
  and and_6 (and_6_out, RegWrite, decoder_1_out5);
  and and_7 (and_7_out, RegWrite, decoder_1_out6);
  Adder #(.width(16)) adder_1 (.a(multiplexer_2_out), .b(multiplexer_3_out), .out(adder_1_out));  // open: cin, cout
  Register_part #(.width(16), .trigger("high")) X0 (.D({16{1'b0}}), .Q(X0_q), .clk(and_1_out));  // open: en, clr
  Register_part #(.width(16), .trigger("high")) X1 (.D(multiplexer_1_out), .Q(X1_q), .clk(and_2_out));  // open: en, clr
  Register_part #(.width(16), .trigger("high")) X2 (.D(multiplexer_1_out), .Q(X2_q), .clk(and_3_out));  // open: en, clr
  Register_part #(.width(16), .trigger("high")) X3 (.D(multiplexer_1_out), .Q(X3_q), .clk(and_4_out));  // open: en, clr
  Register_part #(.width(16), .trigger("high")) X4 (.D(multiplexer_1_out), .Q(X4_q), .clk(and_5_out));  // open: en, clr
  Register_part #(.width(16), .trigger("high")) X5 (.D(multiplexer_1_out), .Q(X5_q), .clk(and_6_out));  // open: en, clr
  Register_part #(.width(16), .trigger("high")) X6 (.D(multiplexer_1_out), .Q(X6_q), .clk(and_7_out));  // open: en, clr
  Register_part #(.width(16), .trigger("falling")) X7 (.D(adder_1_out), .Q(PC), .clk(Clock));  // open: en, clr
  Multiplexer #(.width(3), .enable("false")) multiplexer_4 (
    .in0(Rs_1), .in1(Rd), .out(multiplexer_4_out), .sel(IsSingleReg));
  Multiplexer #(.select(3), .width(16), .enable("false")) multiplexer_5 (
    .in0(X0_q), .in1(X1_q), .in2(X2_q), .in3(X3_q), .in4(X4_q), .in5(X5_q), .in6(X6_q), .out(Read_Data_2),
    .sel(Rs_2));  // open: in7
  Multiplexer #(.select(3), .width(16), .enable("false")) multiplexer_6 (
    .in0(X0_q), .in1(X1_q), .in2(X2_q), .in3(X3_q), .in4(X4_q), .in5(X5_q), .in6(X6_q), .out(Dead_Data1),
    .sel(multiplexer_4_out));  // open: in7
  Decoder #(.select(4), .enable("false")) decoder_2 (
    .out0(ADD), .out1(ADDM), .out2(SUB), .out3(SUBM), .out4(AND), .out5(SHL), .out6(SHRA), .out7(OR),
    .out8(NOT), .out9(LD), .out10(ST), .out11(BR), .out12(JSR), .out13(RTS), .out14(CLK), .out15(LPSW),
    .sel(OpCode));

  // Other names for the same wires on the sheet: GPR[15:0] = Dead_Data1
endmodule

module ALU (
  input  [15:0] Rs2,
  input  [15:0] Rs1,
  input  [3:0] ALU_Op,
  output [15:0] ALU_Result,
  output Zero_Bit,
  output Negative_Bit
);

  wire [15:0] adder_1_out, and_1_out, not_1_out, or_1_out, shifter_1_out, shifter_2_out, subtractor_1_out;

  Adder #(.width(16)) adder_1 (.a(Rs1), .b(Rs2), .out(adder_1_out));  // open: cin, cout
  Subtractor #(.width(16)) subtractor_1 (.a(Rs1), .b(Rs2), .out(subtractor_1_out));  // open: bin, bout
  assign and_1_out = Rs1 & Rs2;  // AND_Gate and_1, 16 bits wide
  assign or_1_out = Rs1 | Rs2;  // OR_Gate or_1, 16 bits wide
  assign not_1_out = ~Rs1;  // NOT_Gate not_1, 16 bits wide
  Shifter #(.width(16)) shifter_1 (.in(Rs1), .\dist (Rs2[3:0]), .out(shifter_1_out));
  Shifter #(.width(16), .shift("lr")) shifter_2 (.in(Rs1), .\dist (Rs2[3:0]), .out(shifter_2_out));
  Multiplexer #(.select(4), .width(16), .enable("false")) multiplexer_1 (
    .in0(adder_1_out), .in1(subtractor_1_out), .in2(and_1_out), .in3(or_1_out), .in4(not_1_out),
    .in5(shifter_1_out), .in6(shifter_2_out), .out(ALU_Result), .sel(ALU_Op));  // open: in7, in8, in9, in10, in11, in12, in13, in14, in15
  nor nor_1 (Zero_Bit, ALU_Result[0], ALU_Result[1], ALU_Result[2], ALU_Result[3], ALU_Result[4], ALU_Result[5], ALU_Result[6], ALU_Result[7], ALU_Result[9], ALU_Result[10], ALU_Result[11], ALU_Result[12], ALU_Result[13], ALU_Result[14], ALU_Result[15], ALU_Result[8]);

  assign Negative_Bit = ALU_Result[15];
endmodule

module ID (
  input  [15:0] Instruction_IN,
  output [6:0] Short_Offset,
  output [3:0] OpCode,
  output [2:0] Rd,
  output N,
  output Z,
  output [2:0] Rs2,
  output [2:0] Rs1,
  output S,
  output [9:0] Long_Offset
);

  wire ADD, ADDM, AND, BR, CLK, JSR, LD, LPSW, NOT, OR, or_1_out, RTS, SHL, SHRA, ST, SUB, SUBM;

  Decoder #(.select(4), .enable("false")) decoder_1 (
    .out0(ADD), .out1(ADDM), .out2(SUB), .out3(SUBM), .out4(AND), .out5(SHL), .out6(SHRA), .out7(OR),
    .out8(NOT), .out9(LD), .out10(ST), .out11(BR), .out12(JSR), .out13(RTS), .out14(CLK), .out15(LPSW),
    .sel(Instruction_IN[13:10]));
  Multiplexer #(.width(3), .enable("false")) multiplexer_1 (
    .in0(Instruction_IN[8:6]), .in1(Instruction_IN[9:7]), .out(Rd), .sel(or_1_out));
  or or_1 (or_1_out, JSR, LD, RTS, SUBM, ADDM, ST, NOT);

  assign Long_Offset = Instruction_IN[9:0];
  assign N = Instruction_IN[14];
  assign OpCode = Instruction_IN[13:10];
  assign Rs1 = Instruction_IN[5:3];
  assign Rs2 = Instruction_IN[2:0];
  assign S = Instruction_IN[9];
  assign Short_Offset = Instruction_IN[6:0];
  assign Z = Instruction_IN[15];

  // Other names for the same wires on the sheet: Rd1[2:0] = Instruction_IN[8:6]; Rd2[2:0] = Instruction_IN[9:7]

  // Notes on the sheet:
  //   D-Type
  //   R-Type
  //   B-Type
endmodule

module Control (
  input  ExceptionFound,
  input  Clock,
  input  [1:0] Step,
  input  Privilaged,
  input  [3:0] OpCode,
  output ALUSrc,
  output Branch,
  output PCV,
  output IsSingleReg,
  output M_Type,
  output [3:0] ALUOp,
  output M_Op,
  output JSR_Op,
  output Timer_Overwrite,
  output PSW_Overwrite,
  output Stage_1,
  output Stage_2,
  output Stage_3,
  output Stage_4,
  output MemWrite,
  output RegWrite,
  output MemtoReg
);

  wire ADD, ADDM, AND, and_2_out, BR, DType, LD, LPSW, nor_1_out, NOT, OR, or_4_out, RTS, RType, SHL, SHRA,
       ST, SUB, xor_1_out;
  wire [1:0] adder_1_out, controlled_buffer_1_out, register_1_q;

  Decoder #(.select(4), .enable("false")) decoder_1 (
    .out0(ADD), .out1(ADDM), .out2(SUB), .out3(M_Op), .out4(AND), .out5(SHL), .out6(SHRA), .out7(OR),
    .out8(NOT), .out9(LD), .out10(ST), .out11(BR), .out12(JSR_Op), .out13(RTS), .out14(Timer_Overwrite),
    .out15(LPSW), .sel(OpCode));
  or or_1 (RegWrite, ADD, ADDM, SUB, M_Op, AND, SHL, SHRA, OR, NOT, LD, JSR_Op);
  or or_2 (MemtoReg, ADDM, M_Op, NOT, LD);
  xor xor_1 (xor_1_out, Step[0], Step[1]);
  or or_3 (MemWrite, xor_1_out, ST);
  Multiplexer #(.select(4), .width(4)) multiplexer_1 (
    .in0(4'b0000), .in1(4'b0000), .in2(4'b0001), .in3(4'b0001), .in4(4'b0010), .in5(4'b0101), .in6(4'b0110),
    .in7(4'b0011), .in8(4'b0100), .in9(4'b0000), .in10(4'b0000), .in11(4'b0000), .in12(4'b0000),
    .in13(4'b0000), .in14(4'b0000), .in15(4'b0000), .out(ALUOp), .sel(OpCode));  // open: en
  or or_4 (or_4_out, Timer_Overwrite, LPSW);
  or or_5 (DType, ADDM, M_Op, NOT, LD, ST, JSR_Op, RTS);
  and and_1 (PCV, or_4_out, ~Privilaged);  // AND_Gate
  or or_6 (Branch, BR, Timer_Overwrite);
  or or_7 (RType, ADD, SUB, AND, SHL, SHRA, OR);
  nor nor_1 (nor_1_out, Step[0], Step[1]);
  assign controlled_buffer_1_out = Clock ? register_1_q : 2'bz;  // Controlled_Buffer controlled_buffer_1
  Adder #(.width(2)) adder_1 (.a(controlled_buffer_1_out), .b(2'b01), .out(adder_1_out));  // open: cin, cout
  Register_part #(.width(2), .trigger("falling")) register_1 (
    .D(adder_1_out), .Q(register_1_q), .clk(Clock));  // open: en, clr
  and and_2 (and_2_out, ExceptionFound, nor_1_out);
  Decoder #(.select(2)) decoder_2 (
    .out0(Stage_1), .out1(Stage_2), .out2(Stage_3), .out3(Stage_4), .sel(register_1_q));  // open: en
  not not_1 (ALUSrc, RType);
  not not_2 (IsSingleReg, RType);
  or or_8 (M_Type, ADDM, M_Op);
  or or_9 (PSW_Overwrite, LPSW, and_2_out);

  // Other names for the same wires on the sheet: BType = Branch; CLK = Timer_Overwrite; JSR = JSR_Op; SUBM = M_Op
endmodule

module CountdownTimer (
  input  [15:0] TimerSetVal,
  input  TimerOverwrite,
  input  Clock,
  output [15:0] Timer_Output
);

  wire [15:0] multiplexer_1_out, subtractor_1_out;

  Subtractor #(.width(16)) subtractor_1 (.a(Timer_Output), .b(16'h1), .out(subtractor_1_out));  // open: bin, bout
  Multiplexer #(.width(16), .enable("false")) multiplexer_1 (
    .in0(subtractor_1_out), .in1(TimerSetVal), .out(multiplexer_1_out), .sel(TimerOverwrite));
  Register_part #(.width(16), .trigger("falling")) register_1 (
    .D(multiplexer_1_out), .Q(Timer_Output), .clk(Clock));  // open: en, clr
endmodule

module ID_EX_Reg (
  input  Clock,
  input  Enable,
  input  WB_IN,
  input  M_IN,
  input  EX_IN,
  input  [15:0] PC_IN,
  input  [15:0] Read_Data1_IN,
  input  [15:0] Read_Data2_IN,
  input  [15:0] Extended_Data_IN,
  input  [10:0] Temp1_IN,
  input  [3:0] OpCode_IN,
  output WB_OUT,
  output M_OUT,
  output EX_OUT,
  output [15:0] PC_OUT,
  output [15:0] Read_Data1_OUT,
  output [15:0] Read_Data2_Out,
  output [15:0] Extended_Data_OUT,
  output [10:0] Temp1_OUT,
  output [3:0] OpCode_OUT
);

  wire register_1_q, register_2_q, register_3_q;
  wire [3:0] register_9_q;
  wire [10:0] register_8_q;
  wire [15:0] register_4_q, register_5_q, register_6_q, register_7_q;

  Register_part #(.width(1), .trigger("falling")) register_1 (
    .D(WB_IN), .en(Enable), .Q(register_1_q), .clk(Clock));  // open: clr
  Register_part #(.width(1), .trigger("falling")) register_2 (
    .D(M_IN), .en(Enable), .Q(register_2_q), .clk(Clock));  // open: clr
  Register_part #(.width(1), .trigger("falling")) register_3 (
    .D(EX_IN), .en(Enable), .Q(register_3_q), .clk(Clock));  // open: clr
  Register_part #(.width(16), .trigger("falling")) register_4 (
    .D(PC_IN), .en(Enable), .Q(register_4_q), .clk(Clock));  // open: clr
  Register_part #(.width(16), .trigger("falling")) register_5 (
    .D(Read_Data1_IN), .en(Enable), .Q(register_5_q), .clk(Clock));  // open: clr
  Register_part #(.width(16), .trigger("falling")) register_6 (
    .D(Read_Data2_IN), .en(Enable), .Q(register_6_q), .clk(Clock));  // open: clr
  Register_part #(.width(16), .trigger("falling")) register_7 (
    .D(Extended_Data_IN), .en(Enable), .Q(register_7_q), .clk(Clock));  // open: clr
  Register_part #(.width(11), .trigger("falling")) register_8 (
    .D(Temp1_IN), .en(Enable), .Q(register_8_q), .clk(Clock));  // open: clr
  Register_part #(.width(4), .trigger("falling")) register_9 (
    .D(OpCode_IN), .en(Enable), .Q(register_9_q), .clk(Clock));  // open: clr
  Register_part #(.width(1)) register_10 (.D(register_1_q), .en(Enable), .Q(WB_OUT), .clk(Clock));  // open: clr
  Register_part #(.width(1)) register_11 (.D(register_2_q), .en(Enable), .Q(M_OUT), .clk(Clock));  // open: clr
  Register_part #(.width(1)) register_12 (.D(register_3_q), .en(Enable), .Q(EX_OUT), .clk(Clock));  // open: clr
  Register_part #(.width(16)) register_13 (.D(register_4_q), .en(Enable), .Q(PC_OUT), .clk(Clock));  // open: clr
  Register_part #(.width(16)) register_14 (
    .D(register_5_q), .en(Enable), .Q(Read_Data1_OUT), .clk(Clock));  // open: clr
  Register_part #(.width(16)) register_15 (
    .D(register_6_q), .en(Enable), .Q(Read_Data2_Out), .clk(Clock));  // open: clr
  Register_part #(.width(16)) register_16 (
    .D(register_7_q), .en(Enable), .Q(Extended_Data_OUT), .clk(Clock));  // open: clr
  Register_part #(.width(11)) register_17 (.D(register_8_q), .en(Enable), .Q(Temp1_OUT), .clk(Clock));  // open: clr
  Register_part #(.width(4)) register_18 (.D(register_9_q), .en(Enable), .Q(OpCode_OUT), .clk(Clock));  // open: clr

  // Other names for the same wires on the sheet: Extended_Data1_IN[15:0] = Extended_Data_IN;
  //   Extended_Data1_OUT[15:0] = Extended_Data_OUT
endmodule

module EX_MEM_Reg (
  input  Clock,
  input  Enable,
  input  WB_IN,
  input  M_IN,
  input  [15:0] PC_IN,
  input  Zero_IN,
  input  Negative_IN,
  input  [15:0] ALU_Res_IN,
  input  [15:0] Temp1_IN,
  output WB_OUT,
  output M_OUT,
  output [15:0] PC_OUT,
  output Zero_OUT,
  output Negative_OUT,
  output [15:0] ALU_Res_OUT,
  output [15:0] Temp1_OUT
);

  wire register_1_q, register_2_q, register_4_q, register_5_q;
  wire [15:0] register_3_q, register_6_q, register_7_q;

  Register_part #(.width(1), .trigger("falling")) register_1 (
    .D(WB_IN), .en(Enable), .Q(register_1_q), .clk(Clock));  // open: clr
  Register_part #(.width(1), .trigger("falling")) register_2 (
    .D(M_IN), .en(Enable), .Q(register_2_q), .clk(Clock));  // open: clr
  Register_part #(.width(16), .trigger("falling")) register_3 (
    .D(PC_IN), .en(Enable), .Q(register_3_q), .clk(Clock));  // open: clr
  Register_part #(.width(1), .trigger("falling")) register_4 (
    .D(Zero_IN), .en(Enable), .Q(register_4_q), .clk(Clock));  // open: clr
  Register_part #(.width(1), .trigger("falling")) register_5 (
    .D(Negative_IN), .en(Enable), .Q(register_5_q), .clk(Clock));  // open: clr
  Register_part #(.width(16), .trigger("falling")) register_6 (
    .D(ALU_Res_IN), .en(Enable), .Q(register_6_q), .clk(Clock));  // open: clr
  Register_part #(.width(16), .trigger("falling")) register_7 (
    .D(Temp1_IN), .en(Enable), .Q(register_7_q), .clk(Clock));  // open: clr
  Register_part #(.width(1)) register_8 (.D(register_1_q), .en(Enable), .Q(WB_OUT), .clk(Clock));  // open: clr
  Register_part #(.width(1)) register_9 (.D(register_2_q), .en(Enable), .Q(M_OUT), .clk(Clock));  // open: clr
  Register_part #(.width(16)) register_10 (.D(register_3_q), .en(Enable), .Q(PC_OUT), .clk(Clock));  // open: clr
  Register_part #(.width(1)) register_11 (.D(register_4_q), .en(Enable), .Q(Zero_OUT), .clk(Clock));  // open: clr
  Register_part #(.width(1)) register_12 (.D(register_5_q), .en(Enable), .Q(Negative_OUT), .clk(Clock));  // open: clr
  Register_part #(.width(16)) register_13 (.D(register_6_q), .en(Enable), .Q(ALU_Res_OUT), .clk(Clock));  // open: clr
  Register_part #(.width(16)) register_14 (.D(register_7_q), .en(Enable), .Q(Temp1_OUT), .clk(Clock));  // open: clr
endmodule

module MEM_WB_Reg (
  input  Clock,
  input  Enable,
  input  WB_IN,
  input  [15:0] ReadData_IN,
  input  [15:0] ALURes_IN,
  output WB_OUT,
  output [15:0] ReadData_OUT,
  output [15:0] ALURes_OUT
);

  wire register_1_q;
  wire [15:0] register_2_q, register_3_q;

  Register_part #(.width(1), .trigger("falling")) register_1 (
    .D(WB_IN), .en(Enable), .Q(register_1_q), .clk(Clock));  // open: clr
  Register_part #(.width(16), .trigger("falling")) register_2 (
    .D(ReadData_IN), .en(Enable), .Q(register_2_q), .clk(Clock));  // open: clr
  Register_part #(.width(16), .trigger("falling")) register_3 (
    .D(ALURes_IN), .en(Enable), .Q(register_3_q), .clk(Clock));  // open: clr
  Register_part #(.width(1)) register_4 (.D(register_1_q), .en(Enable), .Q(WB_OUT), .clk(Clock));  // open: clr
  Register_part #(.width(16)) register_5 (.D(register_2_q), .en(Enable), .Q(ReadData_OUT), .clk(Clock));  // open: clr
  Register_part #(.width(16)) register_6 (.D(register_3_q), .en(Enable), .Q(ALURes_OUT), .clk(Clock));  // open: clr
endmodule

module IF_ID_Reg (
  input  Clock,
  input  Enable,
  input  [15:0] Instruction_IN,
  input  [15:0] PC_IN,
  output [15:0] Instruction_OUT,
  output [15:0] PC_OUT
);

  wire [15:0] register_1_q, register_2_q;

  Register_part #(.width(16), .trigger("falling")) register_1 (
    .D(Instruction_IN), .en(Enable), .Q(register_1_q), .clk(Clock));  // open: clr
  Register_part #(.width(16), .trigger("falling")) register_2 (
    .D(PC_IN), .en(Enable), .Q(register_2_q), .clk(Clock));  // open: clr
  Register_part #(.width(16)) register_3 (
    .D(register_1_q), .en(Enable), .Q(Instruction_OUT), .clk(Clock));  // open: clr
  Register_part #(.width(16)) register_4 (.D(register_2_q), .en(Enable), .Q(PC_OUT), .clk(Clock));  // open: clr
endmodule

module Reg (
  input  RegWrite,
  input  Clock,
  input  IsSingleReg,
  input  [2:0] Rs_1,
  input  [2:0] Rd,
  input  [15:0] Write_Data,
  input  [2:0] Rs_2,
  input  [3:0] OpCode,
  input  [15:0] Extended,
  output [15:0] Read_Data1,
  output [15:0] Read_Data_2,
  output [15:0] PC
);

  wire ADD, ADDM, AND, and_1_out, and_2_out, and_3_out, and_4_out, and_5_out, and_6_out, and_7_out, BR, CLK,
       decoder_1_out0, decoder_1_out1, decoder_1_out2, decoder_1_out3, decoder_1_out4, decoder_1_out5,
       decoder_1_out6, JSR, LD, LPSW, NOT, OR, or_1_out, RTS, SHL, SHRA, ST, SUB, SUBM;
  wire [2:0] multiplexer_4_out;
  wire [15:0] adder_1_out, multiplexer_1_out, multiplexer_2_out, multiplexer_3_out, not_1_out, X0_q, X1_q,
       X2_q, X3_q, X4_q, X5_q, X6_q;

  or or_1 (or_1_out, BR, RTS, JSR);
  Decoder #(.select(3)) decoder_1 (
    .out0(decoder_1_out0), .out1(decoder_1_out1), .out2(decoder_1_out2), .out3(decoder_1_out3),
    .out4(decoder_1_out4), .out5(decoder_1_out5), .out6(decoder_1_out6), .sel(Rd), .en(Clock));  // open: out7
  assign not_1_out = ~Write_Data;  // NOT_Gate not_1, 16 bits wide
  Multiplexer #(.width(16), .enable("false")) multiplexer_1 (
    .in0(Write_Data), .in1(not_1_out), .out(multiplexer_1_out), .sel(NOT));
  Multiplexer #(.width(16), .enable("false")) multiplexer_2 (
    .in0(16'h1), .in1(Extended), .out(multiplexer_2_out), .sel(or_1_out));
  Multiplexer #(.width(16), .enable("false")) multiplexer_3 (
    .in0(PC), .in1(Read_Data1), .out(multiplexer_3_out), .sel(RTS));
  and and_1 (and_1_out, RegWrite, decoder_1_out0);
  and and_2 (and_2_out, RegWrite, decoder_1_out1);
  and and_3 (and_3_out, RegWrite, decoder_1_out2);
  and and_4 (and_4_out, RegWrite, decoder_1_out3);
  and and_5 (and_5_out, RegWrite, decoder_1_out4);
  and and_6 (and_6_out, RegWrite, decoder_1_out5);
  and and_7 (and_7_out, RegWrite, decoder_1_out6);
  Adder #(.width(16)) adder_1 (.a(multiplexer_2_out), .b(multiplexer_3_out), .out(adder_1_out));  // open: cin, cout
  Register_part #(.width(16), .trigger("high")) X0 (.D({16{1'b0}}), .Q(X0_q), .clk(and_1_out));  // open: en, clr
  Register_part #(.width(16), .trigger("high")) X1 (.D(multiplexer_1_out), .Q(X1_q), .clk(and_2_out));  // open: en, clr
  Register_part #(.width(16), .trigger("high")) X2 (.D(multiplexer_1_out), .Q(X2_q), .clk(and_3_out));  // open: en, clr
  Register_part #(.width(16), .trigger("high")) X3 (.D(multiplexer_1_out), .Q(X3_q), .clk(and_4_out));  // open: en, clr
  Register_part #(.width(16), .trigger("high")) X4 (.D(multiplexer_1_out), .Q(X4_q), .clk(and_5_out));  // open: en, clr
  Register_part #(.width(16), .trigger("high")) X5 (.D(multiplexer_1_out), .Q(X5_q), .clk(and_6_out));  // open: en, clr
  Register_part #(.width(16), .trigger("high")) X6 (.D(multiplexer_1_out), .Q(X6_q), .clk(and_7_out));  // open: en, clr
  Register_part #(.width(16), .trigger("falling")) X7 (.D(adder_1_out), .Q(PC), .clk(Clock));  // open: en, clr
  Multiplexer #(.width(3), .enable("false")) multiplexer_4 (
    .in0(Rs_1), .in1(Rd), .out(multiplexer_4_out), .sel(IsSingleReg));
  Multiplexer #(.select(3), .width(16), .enable("false")) multiplexer_5 (
    .in0(X0_q), .in1(X1_q), .in2(X2_q), .in3(X3_q), .in4(X4_q), .in5(X5_q), .in6(X6_q), .out(Read_Data_2),
    .sel(Rs_2));  // open: in7
  Multiplexer #(.select(3), .width(16), .enable("false")) multiplexer_6 (
    .in0(X0_q), .in1(X1_q), .in2(X2_q), .in3(X3_q), .in4(X4_q), .in5(X5_q), .in6(X6_q), .out(Read_Data1),
    .sel(multiplexer_4_out));  // open: in7
  Decoder #(.select(4), .enable("false")) decoder_2 (
    .out0(ADD), .out1(ADDM), .out2(SUB), .out3(SUBM), .out4(AND), .out5(SHL), .out6(SHRA), .out7(OR),
    .out8(NOT), .out9(LD), .out10(ST), .out11(BR), .out12(JSR), .out13(RTS), .out14(CLK), .out15(LPSW),
    .sel(OpCode));

  // Other names for the same wires on the sheet: GPR[15:0] = Read_Data1
endmodule
