// Logisim project test.circ as structural Verilog: 11 circuits, main circuit main
module main (
  input  in_1,
  output [15:0] Result
);

  wire ALU_N, ALU_Z, Clock, EXMEM_MemWrite, EXMEM_RegWrite, IDEX_MemWrite, IDEX_RegWrite, IsSingleReg,
       MemtoReg, MEMWB_RegWrite, MemWrite, N, not_1_out, RegWrite, S, Stage_1, Stage_2, Stage_3, Stage_4,
       Temp0, Temp4, Temp9, Z;
  wire [2:0] Rd, Rs1, Rs2;
  wire [3:0] ALUOp, OpCode, Temp12, Temp13;
  wire [6:0] Short_Offset;
  wire [9:0] Long_Offset;
  wire [10:0] Temp6, Temp11;
  wire [15:0] adder_1_out, ALU_Res, IF_ID_instruction_out, IFID_PC_O, MemAddress, MEMWB_ALU_Res,
       MEMWB_Read_Data, Output_Data_1, PC, Read_Data1, Read_Data2, rom_1_data, Temp1, Temp5, Temp10, Temp15,
       Temp16, Temp19, Temp20, Temp23, Temp24;

  Clock clock_1 (.out(Clock));
  Adder #(.width(16)) adder_1 (.a(PC), .b(16'h1), .out(adder_1_out));  // open: cin, cout
  Control2 Control (
    .Stage_1(Stage_1), .Stage_2(Stage_2), .Stage_3(Stage_3), .Stage_4(Stage_4));  // open: Clock, Clock_2, Stage_1_2, Stage_2_2, Stage_3_2, Stage_4_2, Stage_1_3, Stage_2_3, Stage_3_3, Stage_4_3, Stage_1_4, Stage_2_4, Stage_3_4, Stage_4_4, Stage_1_5, Stage_2_5, Stage_3_5, Stage_4_5
  Register_part #(.width(16), .trigger("falling")) u_PC (.D(adder_1_out), .Q(PC), .clk(Clock));  // open: en, clr
  ROM #(.addrWidth(16), .dataWidth(16)) rom_1 (.addr(PC), .data(rom_1_data));  // open: sel
  IF_ID_Reg IF_ID (
    .Enable(Stage_1), .Instruction_IN(rom_1_data), .PC_IN(PC), .Instruction_OUT(IF_ID_instruction_out),
    .PC_OUT(IFID_PC_O));
  // Probe on IF_ID_instruction_out
  ID Instruction_Decoder (
    .Input_Data(IF_ID_instruction_out), .Short_Offset(Short_Offset), .OpCode(OpCode), .Rd(Rd), .N(N), .Z(Z),
    .Rs2(Rs2), .Rs1(Rs1), .S(S), .Long_Offset(Long_Offset));
  Control Control_Unit (
    .Clock(Clock), .OpCode(OpCode), .M_Type(IsSingleReg), .ALUOp(ALUOp), .Stage_1(Stage_1),
    .Stage_2(Stage_2), .Stage_3(Stage_3), .Stage_4(Stage_4), .MemWrite(MemWrite), .RegWrite(RegWrite),
    .MemtoReg(MemtoReg));  // open: ExceptionFound, Step, Privilaged, ALUSrc, Branch, PCV, IsSingleReg, M_Op, JSR_Op, Timer_Overwrite, PSW_Overwrite
  Register Register_File (
    .Rd(Rd), .Rs_2(Rs2), .Rs_1(Rs1), .IsSingleReg(Temp0), .OpCode(OpCode), .Dead_Data1(Read_Data1),
    .Read_Data_2(Read_Data2), .PC(Temp1));  // open: Clock, Write_Data, Extended, RegWrite
  ID_EX_Reg ID_EX (
    .Enable(Stage_2), .WB_IN(RegWrite), .M_IN(MemWrite), .EX_IN(Temp4), .PC_IN(Temp15),
    .Read_Data1_IN(Read_Data1), .Read_Data2_IN(Read_Data2), .Extended_Data_IN(Temp5), .Temp1_IN(Temp6),
    .Temp2_IN(Temp13), .WB_OUT(IDEX_RegWrite), .M_OUT(IDEX_MemWrite), .EX_OUT(Temp9), .PC_OUT(Temp16),
    .Read_Data1_OUT(Read_Data1), .Read_Data2_Out(Read_Data2), .Extended_Data_OUT(Temp10), .Temp1_OUT(Temp11),
    .Temp2_OUT(Temp13));
  // ALU alu_1: pin names not known; wires that end beside it: Read_Data1, Read_Data2, Temp12, ALU_N, ALU_Z, ALU_Res
  EX_MEM_Reg EX_MEM (
    .Enable(Stage_3), .WB_IN(IDEX_RegWrite), .M_IN(IDEX_MemWrite), .PC_IN(Temp19), .Zero_IN(ALU_Z),
    .Negative_IN(ALU_N), .ALU_Res_IN(ALU_Res), .Temp1_IN(Temp20), .WB_OUT(EXMEM_RegWrite),
    .M_OUT(EXMEM_MemWrite), .PC_OUT(Temp23), .Zero_OUT(ALU_Z), .Negative_OUT(ALU_N), .ALU_Res_OUT(ALU_Res),
    .Temp1_OUT(Temp24));
  assign Result = EXMEM_MemWrite ? Output_Data_1 : 16'bz;  // Controlled_Buffer controlled_buffer_1
  not not_1 (not_1_out, EXMEM_MemWrite);
  RAM #(.addrWidth(16), .dataWidth(16)) ram_1 (
    .addr(MemAddress), .data(Result), .sel(1'b1), .clk(Clock), .ld(not_1_out), .clr(in_1));
  MEM_WB_Reg MEM_WB (
    .Enable(Stage_4), .WB_IN(EXMEM_RegWrite), .ReadData_IN(Result), .ALURes_IN(ALU_Res),
    .WB_OUT(MEMWB_RegWrite), .ReadData_OUT(MEMWB_Read_Data), .ALURes_OUT(MEMWB_ALU_Res));

  // Other names for the same wires on the sheet: Read_Data[15:0] = Result

  // Notes on the sheet:
  //   contents of rom_1 (hex, n*v repeats v):
  //   2484 2508 2883 2907 ca
endmodule

module Register (
  input  RegWrite,
  input  Clock,
  input  [2:0] Rd,
  input  [2:0] Rs_2,
  input  [15:0] Write_Data,
  input  [2:0] Rs_1,
  input  IsSingleReg,
  input  [15:0] Extended,
  input  [3:0] OpCode,
  output [15:0] Dead_Data1,
  output [15:0] Read_Data_2,
  output [15:0] PC
);

  wire ADD, ADDM, AND, and_1_out, and_2_out, and_3_out, and_4_out, and_5_out, and_6_out, and_7_out, BR, CLK,
       decoder_1_out0, decoder_1_out1, decoder_1_out2, decoder_1_out3, decoder_1_out4, decoder_1_out5,
       decoder_1_out6, JSR, LD, LPSW, NOT, OR, or_1_out, RTS, SHL, SHRA, ST, SUB, SUBM;
  wire [2:0] multiplexer_6_out;
  wire [15:0] adder_1_out, multiplexer_1_out, multiplexer_2_out, multiplexer_3_out, not_1_out, X0_q, X1_q,
       X2_q, X3_q, X4_q, X5_q, X6_q;

  or or_1 (or_1_out, BR, RTS, JSR);
  Decoder #(.select(3)) decoder_1 (
    .out0(decoder_1_out0), .out1(decoder_1_out1), .out2(decoder_1_out2), .out3(decoder_1_out3),
    .out4(decoder_1_out4), .out5(decoder_1_out5), .out6(decoder_1_out6), .sel(Rd), .en(Clock));  // open: out7
  assign not_1_out = ~Write_Data;  // NOT_Gate not_1, 16 bits wide
  Multiplexer #(.width(16), .enable("false")) multiplexer_1 (
    .in0(Write_Data), .in1(not_1_out), .out(multiplexer_1_out), .sel(NOT));
  Multiplexer #(.width(16), .enable("false")) multiplexer_2 (
    .in0(16'h1), .in1(Extended), .out(multiplexer_2_out), .sel(or_1_out));
  Multiplexer #(.width(16), .enable("false")) multiplexer_3 (
    .in0(PC), .in1(Dead_Data1), .out(multiplexer_3_out), .sel(RTS));
  and and_1 (and_1_out, RegWrite, decoder_1_out0);
  and and_2 (and_2_out, RegWrite, decoder_1_out1);
  and and_3 (and_3_out, RegWrite, decoder_1_out2);
  and and_4 (and_4_out, RegWrite, decoder_1_out3);
  and and_5 (and_5_out, RegWrite, decoder_1_out4);
  and and_6 (and_6_out, RegWrite, decoder_1_out5);
  and and_7 (and_7_out, RegWrite, decoder_1_out6);
  Adder #(.width(16)) adder_1 (.a(multiplexer_2_out), .b(multiplexer_3_out), .out(adder_1_out));  // open: cin, cout
  Register_part #(.width(16), .trigger("high")) X0 (.D({16{1'b0}}), .Q(X0_q), .clk(and_1_out));  // open: en, clr
  Register_part #(.width(16), .trigger("high")) X1 (.D(multiplexer_1_out), .Q(X1_q), .clk(and_2_out));  // open: en, clr
  Register_part #(.width(16), .trigger("high")) X2 (.D(multiplexer_1_out), .Q(X2_q), .clk(and_3_out));  // open: en, clr
  Register_part #(.width(16), .trigger("high")) X3 (.D(multiplexer_1_out), .Q(X3_q), .clk(and_4_out));  // open: en, clr
  Register_part #(.width(16), .trigger("high")) X4 (.D(multiplexer_1_out), .Q(X4_q), .clk(and_5_out));  // open: en, clr
  Register_part #(.width(16), .trigger("high")) X5 (.D(multiplexer_1_out), .Q(X5_q), .clk(and_6_out));  // open: en, clr
  Register_part #(.width(16), .trigger("high")) X6 (.D(multiplexer_1_out), .Q(X6_q), .clk(and_7_out));  // open: en, clr
  Register_part #(.width(16), .trigger("falling")) X7 (.D(adder_1_out), .Q(PC), .clk(Clock));  // open: en, clr
  Multiplexer #(.select(3), .width(16), .enable("false")) multiplexer_4 (
    .in0(X0_q), .in1(X1_q), .in2(X2_q), .in3(X3_q), .in4(X4_q), .in5(X5_q), .in6(X6_q), .out(Read_Data_2),
    .sel(Rs_2));  // open: in7
  Multiplexer #(.select(3), .width(16), .enable("false")) multiplexer_5 (
    .in0(X0_q), .in1(X1_q), .in2(X2_q), .in3(X3_q), .in4(X4_q), .in5(X5_q), .in6(X6_q), .out(Dead_Data1),
    .sel(multiplexer_6_out));  // open: in7
  Multiplexer #(.width(3), .enable("false")) multiplexer_6 (
    .in0(Rs_1), .in1(Rd), .out(multiplexer_6_out), .sel(IsSingleReg));
  Decoder #(.select(4), .enable("false")) decoder_2 (
    .out0(ADD), .out1(ADDM), .out2(SUB), .out3(SUBM), .out4(AND), .out5(SHL), .out6(SHRA), .out7(OR),
    .out8(NOT), .out9(LD), .out10(ST), .out11(BR), .out12(JSR), .out13(RTS), .out14(CLK), .out15(LPSW),
    .sel(OpCode));

  // Other names for the same wires on the sheet: GPR[15:0] = Dead_Data1
endmodule

module ALU (
  input  [15:0] Rs2,
  input  [15:0] Rs1,
  input  [3:0] ALU_Op,
  output [15:0] ALU_Result,
  output Zero_Bit,
  output Negative_Bit
);

  wire [15:0] adder_1_out, and_1_out, not_1_out, or_1_out, shifter_1_out, shifter_2_out, subtractor_1_out;

  Adder #(.width(16)) adder_1 (.a(Rs1), .b(Rs2), .out(adder_1_out));  // open: cin, cout
  Subtractor #(.width(16)) subtractor_1 (.a(Rs1), .b(Rs2), .out(subtractor_1_out));  // open: bin, bout
  assign and_1_out = Rs1 & Rs2;  // AND_Gate and_1, 16 bits wide
  assign or_1_out = Rs1 | Rs2;  // OR_Gate or_1, 16 bits wide
  assign not_1_out = ~Rs1;  // NOT_Gate not_1, 16 bits wide
  Shifter #(.width(16)) shifter_1 (.in(Rs1), .\dist (Rs2[3:0]), .out(shifter_1_out));
  Shifter #(.width(16), .shift("lr")) shifter_2 (.in(Rs1), .\dist (Rs2[3:0]), .out(shifter_2_out));
  Multiplexer #(.select(4), .width(16), .enable("false")) multiplexer_1 (
    .in0(adder_1_out), .in1(subtractor_1_out), .in2(and_1_out), .in3(or_1_out), .in4(not_1_out),
    .in5(shifter_1_out), .in6(shifter_2_out), .out(ALU_Result), .sel(ALU_Op));  // open: in7, in8, in9, in10, in11, in12, in13, in14, in15
  nor nor_1 (Zero_Bit, ALU_Result[0], ALU_Result[1], ALU_Result[2], ALU_Result[3], ALU_Result[4], ALU_Result[5], ALU_Result[6], ALU_Result[7], ALU_Result[9], ALU_Result[10], ALU_Result[11], ALU_Result[12], ALU_Result[13], ALU_Result[14], ALU_Result[15], ALU_Result[8]);

  assign Negative_Bit = ALU_Result[15];
endmodule

module ID (
  input  [15:0] Input_Data,
  output [6:0] Short_Offset,
  output [3:0] OpCode,
  output [2:0] Rd,
  output N,
  output Z,
  output [2:0] Rs2,
  output [2:0] Rs1,
  output S,
  output [9:0] Long_Offset
);

  wire ADD, ADDM, AND, BR, CLK, JSR, LD, LPSW, NOT, OR, or_1_out, RTS, SHL, SHRA, ST, SUB, SUBM;

  Decoder #(.select(4), .enable("false")) decoder_1 (
    .out0(ADD), .out1(ADDM), .out2(SUB), .out3(SUBM), .out4(AND), .out5(SHL), .out6(SHRA), .out7(OR),
    .out8(NOT), .out9(LD), .out10(ST), .out11(BR), .out12(JSR), .out13(RTS), .out14(CLK), .out15(LPSW),
    .sel(Input_Data[13:10]));
  Multiplexer #(.width(3), .enable("false")) multiplexer_1 (
    .in0(Input_Data[8:6]), .in1(Input_Data[9:7]), .out(Rd), .sel(or_1_out));
  or or_1 (or_1_out, JSR, LD, RTS, SUBM, ADDM, ST, NOT);

  assign Long_Offset = Input_Data[9:0];
  assign N = Input_Data[14];
  assign OpCode = Input_Data[13:10];
  assign Rs1 = Input_Data[5:3];
  assign Rs2 = Input_Data[2:0];
  assign S = Input_Data[9];
  assign Short_Offset = Input_Data[6:0];
  assign Z = Input_Data[15];

  // Other names for the same wires on the sheet: Rd1[2:0] = Input_Data[8:6]; Rd2[2:0] = Input_Data[9:7]

  // Notes on the sheet:
  //   D-Type
  //   R-Type
  //   B-Type
endmodule

module Control (
  input  ExceptionFound,
  input  Clock,
  input  [1:0] Step,
  input  Privilaged,
  input  [3:0] OpCode,
  output ALUSrc,
  output Branch,
  output PCV,
  output IsSingleReg,
  output M_Type,
  output [3:0] ALUOp,
  output M_Op,
  output JSR_Op,
  output Timer_Overwrite,
  output PSW_Overwrite,
  output Stage_1,
  output Stage_2,
  output Stage_3,
  output Stage_4,
  output MemWrite,
  output RegWrite,
  output MemtoReg
);

  wire ADD, ADDM, AND, and_2_out, BR, DType, LD, LPSW, nor_1_out, NOT, OR, or_4_out, RTS, RType, SHL, SHRA,
       ST, SUB, xor_1_out;
  wire [1:0] adder_1_out, controlled_buffer_1_out, register_1_q;

  Decoder #(.select(4), .enable("false")) decoder_1 (
    .out0(ADD), .out1(ADDM), .out2(SUB), .out3(M_Op), .out4(AND), .out5(SHL), .out6(SHRA), .out7(OR),
    .out8(NOT), .out9(LD), .out10(ST), .out11(BR), .out12(JSR_Op), .out13(RTS), .out14(Timer_Overwrite),
    .out15(LPSW), .sel(OpCode));
  or or_1 (RegWrite, ADD, ADDM, SUB, M_Op, AND, SHL, SHRA, OR, NOT, LD, JSR_Op);
  or or_2 (MemtoReg, ADDM, M_Op, NOT, LD);
  xor xor_1 (xor_1_out, Step[0], Step[1]);
  or or_3 (MemWrite, xor_1_out, ST);
  Multiplexer #(.select(4), .width(4)) multiplexer_1 (
    .in0(4'b0000), .in1(4'b0000), .in2(4'b0001), .in3(4'b0001), .in4(4'b0010), .in5(4'b0101), .in6(4'b0110),
    .in7(4'b0011), .in8(4'b0100), .in9(4'b0000), .in10(4'b0000), .in11(4'b0000), .in12(4'b0000),
    .in13(4'b0000), .in14(4'b0000), .in15(4'b0000), .out(ALUOp), .sel(OpCode));  // open: en
  or or_4 (or_4_out, Timer_Overwrite, LPSW);
  or or_5 (DType, ADDM, M_Op, NOT, LD, ST, JSR_Op, RTS);
  and and_1 (PCV, or_4_out, ~Privilaged);  // AND_Gate
  or or_6 (Branch, BR, Timer_Overwrite);
  or or_7 (RType, ADD, SUB, AND, SHL, SHRA, OR);
  nor nor_1 (nor_1_out, Step[0], Step[1]);
  assign controlled_buffer_1_out = Clock ? register_1_q : 2'bz;  // Controlled_Buffer controlled_buffer_1
  Adder #(.width(2)) adder_1 (.a(controlled_buffer_1_out), .b(2'b01), .out(adder_1_out));  // open: cin, cout
  Register_part #(.width(2), .trigger("falling")) register_1 (
    .D(adder_1_out), .Q(register_1_q), .clk(Clock));  // open: en, clr
  and and_2 (and_2_out, ExceptionFound, nor_1_out);
  Decoder #(.select(2)) decoder_2 (
    .out0(Stage_1), .out1(Stage_2), .out2(Stage_3), .out3(Stage_4), .sel(register_1_q));  // open: en
  not not_1 (ALUSrc, RType);
  not not_2 (IsSingleReg, RType);
  or or_8 (M_Type, ADDM, M_Op);
  or or_9 (PSW_Overwrite, LPSW, and_2_out);

  // Other names for the same wires on the sheet: BType = Branch; CLK = Timer_Overwrite; JSR = JSR_Op; SUBM = M_Op
endmodule

module Count_Down_Timer (
  input  TimerOverwrite,
  input  Clock,
  input  [15:0] TimerSetVal,
  output [15:0] Timer_Output
);

  wire [15:0] multiplexer_1_out, subtractor_1_out;

  Subtractor #(.width(16)) subtractor_1 (.a(Timer_Output), .b(16'h1), .out(subtractor_1_out));  // open: bin, bout
  Register_part #(.width(16), .trigger("falling")) Count_Down_Timer (
    .D(multiplexer_1_out), .Q(Timer_Output), .clk(Clock));  // open: en, clr
  Multiplexer #(.width(16), .enable("false")) multiplexer_1 (
    .in0(subtractor_1_out), .in1(TimerSetVal), .out(multiplexer_1_out), .sel(TimerOverwrite));
endmodule

module ID_EX_Reg (
  input  Enable,
  input  WB_IN,
  input  M_IN,
  input  EX_IN,
  input  [15:0] PC_IN,
  input  [15:0] Read_Data1_IN,
  input  [15:0] Read_Data2_IN,
  input  [15:0] Extended_Data_IN,
  input  [10:0] Temp1_IN,
  input  [3:0] Temp2_IN,
  output WB_OUT,
  output M_OUT,
  output EX_OUT,
  output [15:0] PC_OUT,
  output [15:0] Read_Data1_OUT,
  output [15:0] Read_Data2_Out,
  output [15:0] Extended_Data_OUT,
  output [10:0] Temp1_OUT,
  output [3:0] Temp2_OUT
);

  assign WB_OUT = Enable ? WB_IN : 1'bz;  // Controlled_Buffer controlled_buffer_1
  assign M_OUT = Enable ? M_IN : 1'bz;  // Controlled_Buffer controlled_buffer_2
  assign EX_OUT = Enable ? EX_IN : 1'bz;  // Controlled_Buffer controlled_buffer_3
  assign PC_OUT = Enable ? PC_IN : 16'bz;  // Controlled_Buffer controlled_buffer_4
  assign Read_Data1_OUT = Enable ? Read_Data1_IN : 16'bz;  // Controlled_Buffer controlled_buffer_5
  assign Read_Data2_Out = Enable ? Read_Data2_IN : 16'bz;  // Controlled_Buffer controlled_buffer_6
  assign Extended_Data_OUT = Enable ? Extended_Data_IN : 16'bz;  // Controlled_Buffer controlled_buffer_7
  assign Temp1_OUT = Enable ? Temp1_IN : 11'bz;  // Controlled_Buffer controlled_buffer_8
  assign Temp2_OUT = Enable ? Temp2_IN : 4'bz;  // Controlled_Buffer controlled_buffer_9
endmodule

module EX_MEM_Reg (
  input  Enable,
  input  WB_IN,
  input  M_IN,
  input  [15:0] PC_IN,
  input  Zero_IN,
  input  Negative_IN,
  input  [15:0] ALU_Res_IN,
  input  [15:0] Temp1_IN,
  output WB_OUT,
  output M_OUT,
  output [15:0] PC_OUT,
  output Zero_OUT,
  output Negative_OUT,
  output [15:0] ALU_Res_OUT,
  output [15:0] Temp1_OUT
);

  assign WB_OUT = Enable ? WB_IN : 1'bz;  // Controlled_Buffer controlled_buffer_1
  assign M_OUT = Enable ? M_IN : 1'bz;  // Controlled_Buffer controlled_buffer_2
  assign PC_OUT = Enable ? PC_IN : 16'bz;  // Controlled_Buffer controlled_buffer_3
  assign Zero_OUT = Enable ? Zero_IN : 1'bz;  // Controlled_Buffer controlled_buffer_4
  assign Negative_OUT = Enable ? Negative_IN : 1'bz;  // Controlled_Buffer controlled_buffer_5
  assign ALU_Res_OUT = Enable ? ALU_Res_IN : 16'bz;  // Controlled_Buffer controlled_buffer_6
  assign Temp1_OUT = Enable ? Temp1_IN : 16'bz;  // Controlled_Buffer controlled_buffer_7
endmodule

module IF_ID_Reg (
  input  Enable,
  input  [15:0] Instruction_IN,
  input  [15:0] PC_IN,
  output [15:0] Instruction_OUT,
  output [15:0] PC_OUT
);

  assign Instruction_OUT = Enable ? Instruction_IN : 16'bz;  // Controlled_Buffer controlled_buffer_1
  assign PC_OUT = Enable ? PC_IN : 16'bz;  // Controlled_Buffer controlled_buffer_2
endmodule

module Control2 (
  input  Clock,
  input  Clock_2,
  output Stage_1,
  output Stage_2,
  output Stage_3,
  output Stage_4,
  output Stage_1_2,
  output Stage_2_2,
  output Stage_3_2,
  output Stage_4_2,
  output Stage_1_3,
  output Stage_2_3,
  output Stage_3_3,
  output Stage_4_3,
  output Stage_1_4,
  output Stage_2_4,
  output Stage_3_4,
  output Stage_4_4,
  output Stage_1_5,
  output Stage_2_5,
  output Stage_3_5,
  output Stage_4_5
);

  wire decoder_2_out0, decoder_2_out1, decoder_2_out2, decoder_2_out3;
  wire [1:0] adder_1_out, adder_2_out, adder_3_out, adder_4_out, adder_5_out, adder_6_out,
       controlled_buffer_1_out, controlled_buffer_2_out, controlled_buffer_3_out, controlled_buffer_4_out,
       controlled_buffer_5_out, controlled_buffer_6_out, register_1_q, register_2_q, register_3_q,
       register_4_q, register_5_q, register_6_q;

  assign controlled_buffer_1_out = Clock ? register_1_q : 2'bz;  // Controlled_Buffer controlled_buffer_1
  Adder #(.width(2)) adder_1 (.a(controlled_buffer_1_out), .b(2'b01), .out(adder_1_out));  // open: cin, cout
  assign controlled_buffer_2_out = Clock_2 ? register_2_q : 2'bz;  // Controlled_Buffer controlled_buffer_2
  Adder #(.width(2)) adder_2 (.a(controlled_buffer_2_out), .b(2'b01), .out(adder_2_out));  // open: cin, cout
  Register_part #(.width(2), .trigger("falling")) register_1 (
    .D(adder_1_out), .Q(register_1_q), .clk(Clock));  // open: en, clr
  Register_part #(.width(2), .trigger("falling")) register_2 (
    .D(adder_2_out), .Q(register_2_q), .clk(Clock_2));  // open: en, clr
  Decoder #(.select(2)) decoder_1 (
    .out0(Stage_1), .out1(Stage_2), .out2(Stage_3), .out3(Stage_4), .sel(register_1_q));  // open: en
  Decoder #(.select(2)) decoder_2 (
    .out0(decoder_2_out0), .out1(decoder_2_out1), .out2(decoder_2_out2), .out3(decoder_2_out3),
    .sel(register_2_q));  // open: en
  assign controlled_buffer_3_out = decoder_2_out0 ? register_3_q : 2'bz;  // Controlled_Buffer controlled_buffer_3
  Adder #(.width(2)) adder_3 (.a(controlled_buffer_3_out), .b(2'b01), .out(adder_3_out));  // open: cin, cout
  assign controlled_buffer_4_out = decoder_2_out1 ? register_4_q : 2'bz;  // Controlled_Buffer controlled_buffer_4
  Adder #(.width(2)) adder_4 (.a(controlled_buffer_4_out), .b(2'b01), .out(adder_4_out));  // open: cin, cout
  assign controlled_buffer_5_out = decoder_2_out2 ? register_5_q : 2'bz;  // Controlled_Buffer controlled_buffer_5
  Adder #(.width(2)) adder_5 (.a(controlled_buffer_5_out), .b(2'b01), .out(adder_5_out));  // open: cin, cout
  assign controlled_buffer_6_out = decoder_2_out3 ? register_6_q : 2'bz;  // Controlled_Buffer controlled_buffer_6
  Adder #(.width(2)) adder_6 (.a(controlled_buffer_6_out), .b(2'b01), .out(adder_6_out));  // open: cin, cout
  Register_part #(.width(2), .trigger("falling")) register_3 (
    .D(adder_3_out), .Q(register_3_q), .clk(decoder_2_out0));  // open: en, clr
  Register_part #(.width(2), .trigger("falling")) register_4 (
    .D(adder_4_out), .Q(register_4_q), .clk(decoder_2_out1));  // open: en, clr
  Register_part #(.width(2), .trigger("falling")) register_5 (
    .D(adder_5_out), .Q(register_5_q), .clk(decoder_2_out2));  // open: en, clr
  Register_part #(.width(2), .trigger("falling")) register_6 (
    .D(adder_6_out), .Q(register_6_q), .clk(decoder_2_out3));  // open: en, clr
  Decoder #(.select(2)) decoder_3 (
    .out0(Stage_1_2), .out1(Stage_2_2), .out2(Stage_3_2), .out3(Stage_4_2), .sel(register_3_q));  // open: en
  Decoder #(.select(2)) decoder_4 (
    .out0(Stage_1_3), .out1(Stage_2_3), .out2(Stage_3_3), .out3(Stage_4_3), .sel(register_4_q));  // open: en
  Decoder #(.select(2)) decoder_5 (
    .out0(Stage_1_4), .out1(Stage_2_4), .out2(Stage_3_4), .out3(Stage_4_4), .sel(register_5_q));  // open: en
  Decoder #(.select(2)) decoder_6 (
    .out0(Stage_1_5), .out1(Stage_2_5), .out2(Stage_3_5), .out3(Stage_4_5), .sel(register_6_q));  // open: en
endmodule

module MEM_WB_Reg (
  input  Enable,
  input  WB_IN,
  input  [15:0] ReadData_IN,
  input  [15:0] ALURes_IN,
  output WB_OUT,
  output [15:0] ReadData_OUT,
  output [15:0] ALURes_OUT
);

  assign WB_OUT = Enable ? WB_IN : 1'bz;  // Controlled_Buffer controlled_buffer_1
  assign ReadData_OUT = Enable ? ReadData_IN : 16'bz;  // Controlled_Buffer controlled_buffer_2
  assign ALURes_OUT = Enable ? ALURes_IN : 16'bz;  // Controlled_Buffer controlled_buffer_3
endmodule
