// Logisim project Register_Buffer.circ as structural Verilog: 3 circuits, main circuit main
module main (
  input  in_1,
  output out_2
);

  wire clock_1_out, register_1_q;

  Clock clock_1 (.out(clock_1_out));
  Register #(.width(1), .trigger("falling")) register_1 (
    .D(in_1), .en(1'b1), .Q(register_1_q), .clk(clock_1_out));  // open: clr
  Register #(.width(1)) register_2 (.D(register_1_q), .en(1'b1), .Q(out_2), .clk(clock_1_out));  // open: clr
endmodule

module Buffer (
  input  [15:0] in_1
);

  wire clock_1_out;
  wire [15:0] register_1_q, register_2_q, register_3_q, register_4_q, register_5_q, register_6_q,
       register_7_q;

  Clock clock_1 (.out(clock_1_out));
  Register #(.width(16), .trigger("falling")) register_1 (
    .D(in_1), .en(1'b1), .Q(register_1_q), .clk(clock_1_out));  // open: clr
  Register #(.width(16)) register_2 (.D(register_1_q), .en(1'b1), .Q(register_2_q), .clk(clock_1_out));  // open: clr
  Register #(.width(16), .trigger("falling")) register_3 (
    .D(register_2_q), .en(1'b1), .Q(register_3_q), .clk(clock_1_out));  // open: clr
  Register #(.width(16)) register_4 (.D(register_3_q), .en(1'b1), .Q(register_4_q), .clk(clock_1_out));  // open: clr
  Register #(.width(16), .trigger("falling")) register_5 (
    .D(register_4_q), .en(1'b1), .Q(register_5_q), .clk(clock_1_out));  // open: clr
  Register #(.width(16)) register_6 (.D(register_5_q), .en(1'b1), .Q(register_6_q), .clk(clock_1_out));  // open: clr
  Register #(.width(16), .trigger("falling")) register_7 (
    .D(register_6_q), .en(1'b1), .Q(register_7_q), .clk(clock_1_out));  // open: clr
  Register #(.width(16)) register_8 (.D(register_7_q), .en(1'b1), .clk(clock_1_out));  // open: Q, clr
endmodule

module _4_Register_Buffer (
  input  [15:0] in_1,
  input  [15:0] in_2,
  input  [15:0] in_3,
  input  [15:0] in_4
);

  wire Clock;
  wire [15:0] register_1_q, register_2_q, register_3_q, register_4_q, register_5_q, register_6_q,
       register_7_q, register_8_q, register_9_q, register_10_q, register_11_q, register_12_q, register_13_q,
       register_14_q, register_15_q, register_16_q, register_17_q, register_18_q, register_19_q,
       register_20_q, register_21_q, register_22_q, register_23_q, register_24_q, register_25_q,
       register_26_q, register_27_q, register_28_q;

  Clock clock_1 (.out(Clock));
  Register #(.width(16), .trigger("falling")) register_1 (
    .D(in_1), .en(1'b1), .Q(register_1_q), .clk(Clock));  // open: clr
  Register #(.width(16), .trigger("falling")) register_2 (
    .D(in_2), .en(1'b1), .Q(register_2_q), .clk(Clock));  // open: clr
  Register #(.width(16), .trigger("falling")) register_3 (
    .D(in_3), .en(1'b1), .Q(register_3_q), .clk(Clock));  // open: clr
  Register #(.width(16), .trigger("falling")) register_4 (
    .D(in_4), .en(1'b1), .Q(register_4_q), .clk(Clock));  // open: clr
  Register #(.width(16)) register_5 (.D(register_1_q), .en(1'b1), .Q(register_5_q), .clk(Clock));  // open: clr
  Register #(.width(16)) register_6 (.D(register_2_q), .en(1'b1), .Q(register_6_q), .clk(Clock));  // open: clr
  Register #(.width(16)) register_7 (.D(register_3_q), .en(1'b1), .Q(register_7_q), .clk(Clock));  // open: clr
  Register #(.width(16)) register_8 (.D(register_4_q), .en(1'b1), .Q(register_8_q), .clk(Clock));  // open: clr
  Register #(.width(16), .trigger("falling")) register_9 (
    .D(register_5_q), .en(1'b1), .Q(register_9_q), .clk(Clock));  // open: clr
  Register #(.width(16), .trigger("falling")) register_10 (
    .D(register_6_q), .en(1'b1), .Q(register_10_q), .clk(Clock));  // open: clr
  Register #(.width(16), .trigger("falling")) register_11 (
    .D(register_7_q), .en(1'b1), .Q(register_11_q), .clk(Clock));  // open: clr
  Register #(.width(16), .trigger("falling")) register_12 (
    .D(register_8_q), .en(1'b1), .Q(register_12_q), .clk(Clock));  // open: clr
  Register #(.width(16)) register_13 (.D(register_9_q), .en(1'b1), .Q(register_13_q), .clk(Clock));  // open: clr
  Register #(.width(16)) register_14 (.D(register_10_q), .en(1'b1), .Q(register_14_q), .clk(Clock));  // open: clr
  Register #(.width(16)) register_15 (.D(register_11_q), .en(1'b1), .Q(register_15_q), .clk(Clock));  // open: clr
  Register #(.width(16)) register_16 (.D(register_12_q), .en(1'b1), .Q(register_16_q), .clk(Clock));  // open: clr
  Register #(.width(16), .trigger("falling")) register_17 (
    .D(register_13_q), .en(1'b1), .Q(register_17_q), .clk(Clock));  // open: clr
  Register #(.width(16), .trigger("falling")) register_18 (
    .D(register_14_q), .en(1'b1), .Q(register_18_q), .clk(Clock));  // open: clr
  Register #(.width(16), .trigger("falling")) register_19 (
    .D(register_15_q), .en(1'b1), .Q(register_19_q), .clk(Clock));  // open: clr
  Register #(.width(16), .trigger("falling")) register_20 (
    .D(register_16_q), .en(1'b1), .Q(register_20_q), .clk(Clock));  // open: clr
  Register #(.width(16)) register_21 (.D(register_17_q), .en(1'b1), .Q(register_21_q), .clk(Clock));  // open: clr
  Register #(.width(16)) register_22 (.D(register_18_q), .en(1'b1), .Q(register_22_q), .clk(Clock));  // open: clr
  Register #(.width(16)) register_23 (.D(register_19_q), .en(1'b1), .Q(register_23_q), .clk(Clock));  // open: clr
  Register #(.width(16)) register_24 (.D(register_20_q), .en(1'b1), .Q(register_24_q), .clk(Clock));  // open: clr
  Register #(.width(16), .trigger("falling")) register_25 (
    .D(register_21_q), .en(1'b1), .Q(register_25_q), .clk(Clock));  // open: clr
  Register #(.width(16), .trigger("falling")) register_26 (
    .D(register_22_q), .en(1'b1), .Q(register_26_q), .clk(Clock));  // open: clr
  Register #(.width(16), .trigger("falling")) register_27 (
    .D(register_23_q), .en(1'b1), .Q(register_27_q), .clk(Clock));  // open: clr
  Register #(.width(16), .trigger("falling")) register_28 (
    .D(register_24_q), .en(1'b1), .Q(register_28_q), .clk(Clock));  // open: clr
  Register #(.width(16)) register_29 (.D(register_25_q), .en(1'b1), .clk(Clock));  // open: Q, clr
  Register #(.width(16)) register_30 (.D(register_26_q), .en(1'b1), .clk(Clock));  // open: Q, clr
  Register #(.width(16)) register_31 (.D(register_27_q), .en(1'b1), .clk(Clock));  // open: Q, clr
  Register #(.width(16)) register_32 (.D(register_28_q), .en(1'b1), .clk(Clock));  // open: Q, clr

  // Other names for the same wires on the sheet: Input1[15:0] = in_1; Input2[15:0] = in_2; Input3[15:0] = in_3;
  //   Input4[15:0] = in_4
endmodule
