// Logisim project hazard and forward skeleton.circ as structural Verilog: 3 circuits, main circuit main
module main (
);

  Forwarding forwarding_1 ();  // open: Rn, Rm, EX_MEM_RegisterRd, EX_MEM_WB, MEM_WB_RegisterRd, MEM_WB_WB, ForwardA, ForwardB
  Hazard_Detection hazard_detection_1 ();  // open: Instruction1, Instruction2, ID_EX_MemRead, ID_EX_Rd, ControlMUX, PCWrite, IF_IDWrite
endmodule

module Forwarding (
  input  Rn,
  input  Rm,
  input  EX_MEM_RegisterRd,
  input  EX_MEM_WB,
  input  MEM_WB_RegisterRd,
  input  MEM_WB_WB,
  output ForwardA,
  output ForwardB
);
endmodule

module Hazard_Detection (
  input  Instruction1,
  input  Instruction2,
  input  ID_EX_MemRead,
  input  ID_EX_Rd,
  output ControlMUX,
  output PCWrite,
  output IF_IDWrite
);
endmodule
