// Logisim project projectCircuit2.circ as structural Verilog: 7 circuits, main circuit main
module main (
  input  in_1,
  output [15:0] Result,
  output [15:0] Data_Bus,
  output [9:0] out_4
);

  wire ALUSrc, Branch, Clock, clock_1_out, ExceptionCleared, ExceptionFound, IsSingleReg, JSR_Op, M_Op,
       M_Type, MemtoReg, MemWrite, N, Negative, not_1_out, or_1_out, or_2_out, or_3_out, or_4_out, PCV,
       Privileged_Clock, PSW_N_OUT, PSW_Overwrite, PSW_P_OUT, PSW_Z_OUT, RegWrite, S, Timeout,
       Timer_Overwrite, Z, Zero;
  wire [1:0] Step;
  wire [2:0] Rd, Rs1, Rs2;
  wire [3:0] ALUOp, OpCode;
  wire [6:0] Short_Offset;
  wire [15:0] adder_1_out, adder_2_out, ALU_Result, bit_extender_1_out, bit_extender_2_out,
       Count_Down_Timer_timer_output, ExceptionAddress, ExceptionData, Extended, Long_Extended, MemAddress,
       multiplexer_2_out, multiplexer_3_out, multiplexer_4_out, multiplexer_5_out, multiplexer_6_out,
       multiplexer_9_out, Output_Data_1, Output_Data_2, PC, PSW_Z_IN_q, Short_Extended, subtractor_1_out,
       TempReg_2_q, TempReg_q, WriteDatatoReg;
  wire [15:3] PSW_q;

  Clock clock_1 (.out(clock_1_out));
  Demultiplexer #(.enable("false")) demultiplexer_1 (
    .out0(Clock), .out1(Privileged_Clock), .in(clock_1_out), .sel(or_1_out));
  or or_1 (or_1_out, ExceptionFound, ExceptionCleared);
  Control Control (
    .ExceptionFound(ExceptionFound), .Clock(Clock), .Step(Step), .Privilaged(PSW_P_OUT), .OpCode(OpCode),
    .PCV(PCV), .ALUSrc(ALUSrc), .Branch(Branch), .IsSingleReg(IsSingleReg), .M_Type(M_Type), .M_Op(M_Op),
    .JSR_Op(JSR_Op), .Timer_Overwrite(Timer_Overwrite), .PSW_Overwrite(PSW_Overwrite), .MemWrite(MemWrite),
    .RegWrite(RegWrite), .MemtoReg(MemtoReg), .ALUOp(ALUOp));
  ROM #(.addrWidth(16), .dataWidth(16)) rom_1 (.addr(PC), .data(Data_Bus));  // open: sel
  ID Instruction_Decode (
    .Input_Data(Data_Bus), .Short_Offset(Short_Offset), .OpCode(OpCode), .Rd(Rd), .N(N), .Z(Z), .Rs2(Rs2),
    .Rs1(Rs1), .S(S), .Long_Offset(out_4));
  assign bit_extender_1_out = {{9{1'b0}}, Short_Offset};  // Bit_Extender bit_extender_1
  assign bit_extender_2_out = {{6{1'b0}}, out_4};  // Bit_Extender bit_extender_2
  Register Register (
    .Clock(Clock), .Input_Data(WriteDatatoReg), .Extended(Extended), .RegWrite(RegWrite), .Rd(Rd),
    .Rs_2(Rs2), .OpCode(OpCode), .Rs_1(Rs1), .IsSingleReg(IsSingleReg), .Output_Data_1(Output_Data_1),
    .Output_Data_2(Output_Data_2), .PC(PC));
  Multiplexer #(.width(16), .enable("false")) multiplexer_1 (
    .in0(bit_extender_1_out), .in1(bit_extender_2_out), .out(Extended), .sel(Branch));
  // Probe on Output_Data_1
  // Probe on Output_Data_2
  assign Short_Extended = {{9{1'b0}}, Short_Offset};  // Bit_Extender bit_extender_3
  assign Long_Extended = {{6{1'b0}}, out_4};  // Bit_Extender bit_extender_4
  Register_part #(.width(16)) TempReg (.D(Output_Data_1), .Q(TempReg_q), .clk(Clock));  // open: en, clr
  Register_part #(.width(16)) TempReg_2 (.D(Output_Data_1), .Q(TempReg_2_q), .clk(Clock));  // open: en, clr
  Multiplexer #(.width(16), .enable("false")) multiplexer_2 (
    .in0(Output_Data_2), .in1(Extended), .out(multiplexer_2_out), .sel(ALUSrc));
  Multiplexer #(.width(16), .enable("false")) multiplexer_3 (
    .in0(Output_Data_1), .in1(ExceptionData), .out(multiplexer_3_out), .sel(ExceptionFound));
  Adder #(.width(16)) adder_1 (.a(Result), .b(TempReg_q), .out(adder_1_out));  // open: cin, cout
  Subtractor #(.width(16)) subtractor_1 (.a(TempReg_2_q), .b(Result), .out(subtractor_1_out));  // open: bin, bout
  assign Result = MemWrite ? multiplexer_3_out : 16'bz;  // Controlled_Buffer controlled_buffer_1
  Multiplexer #(.width(16), .enable("false")) multiplexer_4 (
    .in0(adder_1_out), .in1(subtractor_1_out), .out(multiplexer_4_out), .sel(M_Op));
  ALU ALU (
    .Rs1(Output_Data_1), .Rs2(multiplexer_2_out), .op_select(ALUOp), .Negative_Bit(Negative),
    .Zero_Bit(Zero), .ALU_Result(ALU_Result));
  not not_1 (not_1_out, MemWrite);
  Adder #(.width(16)) adder_2 (.a(PC), .b(Extended), .out(adder_2_out));  // open: cin, cout
  Multiplexer #(.width(16), .enable("false")) multiplexer_5 (
    .in0(ALU_Result), .in1(PC), .out(multiplexer_5_out), .sel(JSR_Op));
  RAM #(.addrWidth(16), .dataWidth(16)) ram_1 (
    .addr(MemAddress), .data(Result), .sel(1'b1), .clk(Clock), .ld(not_1_out), .clr(in_1));
  // Probe on MemAddress
  Multiplexer #(.width(16), .enable("false")) multiplexer_6 (
    .in0(Result), .in1(multiplexer_4_out), .out(multiplexer_6_out), .sel(M_Type));
  // Probe on multiplexer_6_out
  Multiplexer #(.width(16), .enable("false")) multiplexer_7 (
    .in0(adder_2_out), .in1(ExceptionAddress), .out(MemAddress), .sel(ExceptionFound));
  Multiplexer #(.width(16), .enable("false")) multiplexer_8 (
    .in0(multiplexer_5_out), .in1(multiplexer_6_out), .out(WriteDatatoReg), .sel(MemtoReg));
  Register_part #(.width(1)) PSW_P_IN (.Q(PSW_Z_IN_q[2]));  // open: D, en, clk, clr
  Register_part #(.width(1), .trigger("falling")) PSW_N_IN (.D(Negative), .Q(PSW_Z_IN_q[1]));  // open: en, clk, clr
  Register_part #(.width(1), .trigger("falling")) PSW_Z_IN (.D(Zero), .Q(PSW_Z_IN_q[0]));  // open: en, clk, clr
  Violation_Handler Violation_Handler (
    .PCV(PCV), .Timeout(Timeout), .Clock(or_2_out), .StepIn(Step), .ExceptionFound(ExceptionFound),
    .StepOut(Step), .ExceptionCleared(ExceptionCleared), .ExceptionAddress(ExceptionAddress));
  or or_2 (or_2_out, Privileged_Clock, Clock);
  Multiplexer #(.width(16), .enable("false")) multiplexer_9 (
    .in0(PSW_Z_IN_q), .in1(Result), .out(multiplexer_9_out), .sel(PSW_Overwrite));
  Register_part #(.width(16), .trigger("high")) PSW (
    .D(multiplexer_9_out), .Q({PSW_q, PSW_P_OUT, PSW_N_OUT, PSW_Z_OUT}), .clk(or_3_out));  // open: en, clr
  or or_3 (or_3_out, Privileged_Clock, Clock);
  Count_Down_Timer Count_Down_Timer (
    .Privilaged(PSW_P_OUT), .TimerSetVal(Result), .TimerOverwrite(Timer_Overwrite), .Clock(or_4_out),
    .Timer_Output(Count_Down_Timer_timer_output), .Timeout(Timeout));
  or or_4 (or_4_out, Privileged_Clock, Clock);
  // Probe on Count_Down_Timer_timer_output

  // Other names for the same wires on the sheet: Long_Offset[9:0] = out_4; Read_Data[15:0] = Result

  // Notes on the sheet:
  //   contents of rom_1 (hex, n*v repeats v):
  //   0 0 3c04
endmodule

module Register (
  input  RegWrite,
  input  Clock,
  input  [2:0] Rd,
  input  [2:0] Rs_2,
  input  [15:0] Input_Data,
  input  [2:0] Rs_1,
  input  IsSingleReg,
  input  [15:0] Extended,
  input  [3:0] OpCode,
  output [15:0] Output_Data_1,
  output [15:0] Output_Data_2,
  output [15:0] PC
);

  wire ADD, ADDM, AND, and_1_out, and_2_out, and_3_out, and_4_out, and_5_out, and_6_out, and_7_out, BR, CLK,
       decoder_1_out0, decoder_1_out1, decoder_1_out2, decoder_1_out3, decoder_1_out4, decoder_1_out5,
       decoder_1_out6, JSR, LD, LPSW, NOT, OR, or_1_out, RTS, SHL, SHRA, ST, SUB, SUBM;
  wire [2:0] multiplexer_6_out;
  wire [15:0] adder_1_out, multiplexer_1_out, multiplexer_2_out, multiplexer_3_out, not_1_out, X0_q, X1_q,
       X2_q, X3_q, X4_q, X5_q, X6_q;

  or or_1 (or_1_out, BR, RTS, JSR);
  Decoder #(.select(3)) decoder_1 (
    .out0(decoder_1_out0), .out1(decoder_1_out1), .out2(decoder_1_out2), .out3(decoder_1_out3),
    .out4(decoder_1_out4), .out5(decoder_1_out5), .out6(decoder_1_out6), .sel(Rd), .en(Clock));  // open: out7
  assign not_1_out = ~Input_Data;  // NOT_Gate not_1, 16 bits wide
  Multiplexer #(.width(16), .enable("false")) multiplexer_1 (
    .in0(Input_Data), .in1(not_1_out), .out(multiplexer_1_out), .sel(NOT));
  Multiplexer #(.width(16), .enable("false")) multiplexer_2 (
    .in0(16'h1), .in1(Extended), .out(multiplexer_2_out), .sel(or_1_out));
  Multiplexer #(.width(16), .enable("false")) multiplexer_3 (
    .in0(PC), .in1(Output_Data_1), .out(multiplexer_3_out), .sel(RTS));
  and and_1 (and_1_out, RegWrite, decoder_1_out0);
  and and_2 (and_2_out, RegWrite, decoder_1_out1);
  and and_3 (and_3_out, RegWrite, decoder_1_out2);
  and and_4 (and_4_out, RegWrite, decoder_1_out3);
  and and_5 (and_5_out, RegWrite, decoder_1_out4);
  and and_6 (and_6_out, RegWrite, decoder_1_out5);
  and and_7 (and_7_out, RegWrite, decoder_1_out6);
  Adder #(.width(16)) adder_1 (.a(multiplexer_2_out), .b(multiplexer_3_out), .out(adder_1_out));  // open: cin, cout
  Register_part #(.width(16), .trigger("high")) X0 (.D({16{1'b0}}), .Q(X0_q), .clk(and_1_out));  // open: en, clr
  Register_part #(.width(16), .trigger("high")) X1 (.D(multiplexer_1_out), .Q(X1_q), .clk(and_2_out));  // open: en, clr
  Register_part #(.width(16), .trigger("high")) X2 (.D(multiplexer_1_out), .Q(X2_q), .clk(and_3_out));  // open: en, clr
  Register_part #(.width(16), .trigger("high")) X3 (.D(multiplexer_1_out), .Q(X3_q), .clk(and_4_out));  // open: en, clr
  Register_part #(.width(16), .trigger("high")) X4 (.D(multiplexer_1_out), .Q(X4_q), .clk(and_5_out));  // open: en, clr
  Register_part #(.width(16), .trigger("high")) X5 (.D(multiplexer_1_out), .Q(X5_q), .clk(and_6_out));  // open: en, clr
  Register_part #(.width(16), .trigger("high")) X6 (.D(multiplexer_1_out), .Q(X6_q), .clk(and_7_out));  // open: en, clr
  Register_part #(.width(16), .trigger("falling")) X7 (.D(adder_1_out), .Q(PC), .clk(Clock));  // open: en, clr
  Multiplexer #(.select(3), .width(16), .enable("false")) multiplexer_4 (
    .in0(X0_q), .in1(X1_q), .in2(X2_q), .in3(X3_q), .in4(X4_q), .in5(X5_q), .in6(X6_q), .out(Output_Data_2),
    .sel(Rs_2));  // open: in7
  Decoder #(.select(4), .enable("false")) decoder_2 (
    .out0(ADD), .out1(ADDM), .out2(SUB), .out3(SUBM), .out4(AND), .out5(SHL), .out6(SHRA), .out7(OR),
    .out8(NOT), .out9(LD), .out10(ST), .out11(BR), .out12(JSR), .out13(RTS), .out14(CLK), .out15(LPSW),
    .sel(OpCode));
  Multiplexer #(.select(3), .width(16), .enable("false")) multiplexer_5 (
    .in0(X0_q), .in1(X1_q), .in2(X2_q), .in3(X3_q), .in4(X4_q), .in5(X5_q), .in6(X6_q), .out(Output_Data_1),
    .sel(multiplexer_6_out));  // open: in7
  Multiplexer #(.width(3), .enable("false")) multiplexer_6 (
    .in0(Rs_1), .in1(Rd), .out(multiplexer_6_out), .sel(IsSingleReg));

  // Other names for the same wires on the sheet: GPR[15:0] = Output_Data_1
endmodule

module ALU (
  input  [15:0] Rs1,
  input  [15:0] Rs2,
  input  [3:0] op_select,
  output Negative_Bit,
  output Zero_Bit,
  output [15:0] ALU_Result
);

  wire [15:0] adder_1_out, and_1_out, divider_1_out, divider_1_rem, multiplier_1_out, nand_1_out, nor_1_out,
       not_1_out, or_1_out, shifter_1_out, shifter_2_out, shifter_3_out, shifter_4_out, shifter_5_out,
       subtractor_1_out, xor_1_out;

  Adder #(.width(16)) adder_1 (.a(Rs1), .b(Rs2), .out(adder_1_out));  // open: cin, cout
  Subtractor #(.width(16)) subtractor_1 (.a(Rs1), .b(Rs2), .out(subtractor_1_out), .bin(1'b0));  // open: bout
  Multiplier #(.width(16)) multiplier_1 (.a(Rs1), .b(Rs2), .out(multiplier_1_out));  // open: cin, cout
  Divider #(.width(16)) divider_1 (.a(Rs1), .b(Rs2), .out(divider_1_out), .rem(divider_1_rem));  // open: upper
  Shifter #(.width(16)) shifter_1 (.in(Rs1), .\dist (Rs2[3:0]), .out(shifter_1_out));
  Shifter #(.width(16), .shift("lr")) shifter_2 (.in(Rs1), .\dist (Rs2[3:0]), .out(shifter_2_out));
  Shifter #(.width(16), .shift("ar")) shifter_3 (.in(Rs1), .\dist (Rs2[3:0]), .out(shifter_3_out));
  Shifter #(.width(16), .shift("rl")) shifter_4 (.in(Rs1), .\dist (Rs2[3:0]), .out(shifter_4_out));
  Shifter #(.width(16), .shift("rr")) shifter_5 (.in(Rs1), .\dist (Rs2[3:0]), .out(shifter_5_out));
  assign and_1_out = Rs1 & Rs2;  // AND_Gate and_1, 16 bits wide
  assign or_1_out = Rs1 | Rs2;  // OR_Gate or_1, 16 bits wide
  assign xor_1_out = Rs1 ^ Rs2;  // XOR_Gate xor_1, 16 bits wide
  assign nand_1_out = ~(Rs1 & Rs2);  // NAND_Gate nand_1, 16 bits wide
  assign nor_1_out = ~(Rs1 | Rs2);  // NOR_Gate nor_1, 16 bits wide
  assign not_1_out = ~Rs1;  // NOT_Gate not_1, 16 bits wide
  Multiplexer #(.select(4), .width(16), .enable("false")) multiplexer_1 (
    .in0(adder_1_out), .in1(subtractor_1_out), .in2(multiplier_1_out), .in3(divider_1_out),
    .in4(divider_1_rem), .in5(and_1_out), .in6(or_1_out), .in7(xor_1_out), .in8(nand_1_out), .in9(nor_1_out),
    .in10(not_1_out), .in11(shifter_1_out), .in12(shifter_2_out), .in13(shifter_3_out), .in14(shifter_4_out),
    .in15(shifter_5_out), .out(ALU_Result), .sel(op_select));
  nor nor_2 (Zero_Bit, ALU_Result[0], ALU_Result[1], ALU_Result[2], ALU_Result[3], ALU_Result[4], ALU_Result[5], ALU_Result[6], ALU_Result[7], ALU_Result[9], ALU_Result[10], ALU_Result[11], ALU_Result[12], ALU_Result[13], ALU_Result[14], ALU_Result[15], ALU_Result[8]);

  assign Negative_Bit = ALU_Result[0];
endmodule

module ID (
  input  [15:0] Input_Data,
  output [6:0] Short_Offset,
  output [3:0] OpCode,
  output [2:0] Rd,
  output N,
  output Z,
  output [2:0] Rs2,
  output [2:0] Rs1,
  output S,
  output [9:0] Long_Offset
);

  wire ADD, ADDM, AND, BR, CLK, JSR, LD, LPSW, NOT, OR, or_1_out, RTS, SHL, SHRA, ST, SUB, SUBM;

  Decoder #(.select(4), .enable("false")) decoder_1 (
    .out0(ADD), .out1(ADDM), .out2(SUB), .out3(SUBM), .out4(AND), .out5(SHL), .out6(SHRA), .out7(OR),
    .out8(NOT), .out9(LD), .out10(ST), .out11(BR), .out12(JSR), .out13(RTS), .out14(CLK), .out15(LPSW),
    .sel(Input_Data[13:10]));
  Multiplexer #(.width(3), .enable("false")) multiplexer_1 (
    .in0(Input_Data[8:6]), .in1(Input_Data[9:7]), .out(Rd), .sel(or_1_out));
  or or_1 (or_1_out, JSR, LD, RTS, SUBM, ADDM, ST, NOT);

  assign Long_Offset = Input_Data[9:0];
  assign N = Input_Data[14];
  assign OpCode = Input_Data[13:10];
  assign Rs1 = Input_Data[5:3];
  assign Rs2 = Input_Data[2:0];
  assign S = Input_Data[9];
  assign Short_Offset = Input_Data[6:0];
  assign Z = Input_Data[15];

  // Other names for the same wires on the sheet: Rd1[2:0] = Input_Data[8:6]; Rd2[2:0] = Input_Data[9:7]

  // Notes on the sheet:
  //   D-Type
  //   R-Type
  //   B-Type
endmodule

module Control (
  input  ExceptionFound,
  input  Clock,
  input  [1:0] Step,
  input  Privilaged,
  input  [3:0] OpCode,
  output PCV,
  output ALUSrc,
  output Branch,
  output IsSingleReg,
  output M_Type,
  output M_Op,
  output JSR_Op,
  output Timer_Overwrite,
  output PSW_Overwrite,
  output MemWrite,
  output RegWrite,
  output MemtoReg,
  output [3:0] ALUOp
);

  wire ADD, ADDM, AND, and_1_out, and_2_out, BR, DType, LD, LPSW, MemtoReg0, MemtoReg2, MemtoReg4, MemtoReg5,
       MemtoReg6, MemtoReg7, MemtoReg8, MemtoReg10, MemtoReg11, MemtoReg12, MemtoReg13, MemtoReg14,
       MemtoReg15, MemWrite0, MemWrite1, MemWrite2, MemWrite3, MemWrite4, MemWrite5, MemWrite6, MemWrite7,
       MemWrite8, MemWrite9, MemWrite10, MemWrite11, MemWrite12, MemWrite13, MemWrite14, MemWrite15,
       nor_1_out, OR, or_3_out, register_1_q, RegWrite2, RegWrite5, RegWrite6, RegWrite10, RegWrite11,
       RegWrite13, RegWrite14, RegWrite15, RTS, RType;

  Decoder #(.select(4), .enable("false")) decoder_1 (
    .out0(ADD), .out1(ADDM), .out2(RegWrite2), .out3(M_Op), .out4(AND), .out5(RegWrite5), .out6(RegWrite6),
    .out7(OR), .out8(MemtoReg8), .out9(LD), .out10(MemWrite10), .out11(BR), .out12(JSR_Op), .out13(RTS),
    .out14(Timer_Overwrite), .out15(LPSW), .sel(OpCode));
  not not_1 (MemWrite0, ADD);
  not not_2 (MemtoReg0, ADD);
  not not_3 (MemWrite1, ADDM);
  not not_4 (MemWrite2, RegWrite2);
  not not_5 (MemtoReg2, RegWrite2);
  not not_6 (MemWrite3, M_Op);
  not not_7 (MemWrite4, AND);
  not not_8 (MemtoReg4, AND);
  not not_9 (MemWrite5, RegWrite5);
  not not_10 (MemtoReg5, RegWrite5);
  or or_1 (RType, ADD, RegWrite2, AND, RegWrite5, RegWrite6, OR);
  not not_11 (MemWrite6, RegWrite6);
  not not_12 (MemtoReg6, RegWrite6);
  not not_13 (MemWrite7, OR);
  not not_14 (MemtoReg7, OR);
  not not_15 (MemWrite8, MemtoReg8);
  not not_16 (MemWrite9, LD);
  not not_17 (RegWrite10, MemWrite10);
  not not_18 (MemtoReg10, MemWrite10);
  not not_19 (RegWrite11, BR);
  not not_20 (MemWrite11, BR);
  not not_21 (MemtoReg11, BR);
  not not_22 (MemWrite12, JSR_Op);
  not not_23 (MemtoReg12, JSR_Op);
  not not_24 (RegWrite13, RTS);
  not not_25 (MemWrite13, RTS);
  not not_26 (MemtoReg13, RTS);
  not not_27 (RegWrite14, Timer_Overwrite);
  not not_28 (MemWrite14, Timer_Overwrite);
  not not_29 (MemtoReg14, Timer_Overwrite);
  not not_30 (RegWrite15, LPSW);
  not not_31 (MemWrite15, LPSW);
  not not_32 (MemtoReg15, LPSW);
  or or_2 (DType, ADDM, M_Op, MemtoReg8, LD, MemWrite10, JSR_Op, RTS);
  or or_3 (or_3_out, Timer_Overwrite, LPSW);
  and and_1 (and_1_out, or_3_out, ~Privilaged);  // AND_Gate
  nor nor_1 (nor_1_out, Step[0], Step[1]);
  Register_part #(.width(1), .trigger("low")) register_1 (.D(PCV), .Q(register_1_q), .clk(Clock));  // open: en, clr
  or or_4 (PCV, register_1_q, and_1_out);
  and and_2 (and_2_out, ExceptionFound, nor_1_out);
  not not_33 (ALUSrc, RType);
  not not_34 (IsSingleReg, RType);
  or or_5 (M_Type, ADDM, M_Op);
  or or_6 (PSW_Overwrite, LPSW, and_2_out);
  Multiplexer #(.select(4)) multiplexer_1 (
    .in0(MemWrite0), .in1(MemWrite1), .in2(MemWrite2), .in3(MemWrite3), .in4(MemWrite4), .in5(MemWrite5),
    .in6(MemWrite6), .in7(MemWrite7), .in8(MemWrite8), .in9(MemWrite9), .in10(MemWrite10), .in11(MemWrite11),
    .in12(MemWrite12), .in13(MemWrite13), .in14(MemWrite14), .in15(MemWrite15), .out(MemWrite), .sel(OpCode));  // open: en
  or or_7 (Branch, BR, Timer_Overwrite);
  Multiplexer #(.select(4)) multiplexer_2 (
    .in0(ADD), .in1(ADDM), .in2(RegWrite2), .in3(M_Op), .in4(AND), .in5(RegWrite5), .in6(RegWrite6),
    .in7(OR), .in8(MemtoReg8), .in9(LD), .in10(RegWrite10), .in11(RegWrite11), .in12(JSR_Op),
    .in13(RegWrite13), .in14(RegWrite14), .in15(RegWrite15), .out(RegWrite), .sel(OpCode));  // open: en
  Multiplexer #(.select(4)) multiplexer_3 (
    .in0(MemtoReg0), .in1(ADDM), .in2(MemtoReg2), .in3(M_Op), .in4(MemtoReg4), .in5(MemtoReg5),
    .in6(MemtoReg6), .in7(MemtoReg7), .in8(MemtoReg8), .in9(LD), .in10(MemtoReg10), .in11(MemtoReg11),
    .in12(MemtoReg12), .in13(MemtoReg13), .in14(MemtoReg14), .in15(MemtoReg15), .out(MemtoReg), .sel(OpCode));  // open: en
  Multiplexer #(.select(4), .width(4)) multiplexer_4 (
    .in0(4'b0000), .in1(4'b0000), .in2(4'b0001), .in3(4'b0001), .in4(4'b0101), .in5(4'b1011), .in6(4'b1100),
    .in7(4'b0110), .in8(4'b1010), .in9(4'b0000), .in10(4'b0000), .in11(4'b0000), .in12(4'b0000),
    .in13(4'b0000), .in14(4'b0000), .in15(4'b0000), .out(ALUOp), .sel(OpCode));  // open: en

  // Other names for the same wires on the sheet: BType = Branch; CLK = Timer_Overwrite; RegWrite0 = ADD;
  //   MemtoReg1 = ADDM; RegWrite1 = ADDM; RegWrite4 = AND; RegWrite7 = OR; NOT = MemtoReg8; RegWrite8 = MemtoReg8;
  //   MemtoReg9 = LD; RegWrite9 = LD; JSR = JSR_Op; RegWrite12 = JSR_Op; SHL = RegWrite5; SHRA = RegWrite6;
  //   ST = MemWrite10; SUB = RegWrite2; MemtoReg3 = M_Op; RegWrite3 = M_Op; SUBM = M_Op
endmodule

module Count_Down_Timer (
  input  TimerOverwrite,
  input  Clock,
  input  [15:0] TimerSetVal,
  input  Privilaged,
  output [15:0] Timer_Output,
  output Timeout
);

  wire nor_1_out;
  wire [15:0] multiplexer_1_out, subtractor_1_out;

  Subtractor #(.width(16)) subtractor_1 (.a(Timer_Output), .b(16'h1), .out(subtractor_1_out));  // open: bin, bout
  Register_part #(.width(16), .trigger("falling")) Count_Down_Timer (
    .D(multiplexer_1_out), .Q(Timer_Output), .clk(Clock));  // open: en, clr
  Multiplexer #(.width(16), .enable("false")) multiplexer_1 (
    .in0(subtractor_1_out), .in1(TimerSetVal), .out(multiplexer_1_out), .sel(TimerOverwrite));
  nor nor_1 (nor_1_out, Timer_Output[0], Timer_Output[1], Timer_Output[2], Timer_Output[3], Timer_Output[4], Timer_Output[5], Timer_Output[6], Timer_Output[7], Timer_Output[8], Timer_Output[9], Timer_Output[10], Timer_Output[11], Timer_Output[12], Timer_Output[13], Timer_Output[14], Timer_Output[15], 1'b0, 1'b0, 1'b0, 1'b0, 1'b0, 1'b0, 1'b0, 1'b0, 1'b0, 1'b0, 1'b0, 1'b0, 1'b0, 1'b0, 1'b0, 1'b0);
  and and_1 (Timeout, nor_1_out, ~Privilaged);  // AND_Gate

  // Other names for the same wires on the sheet: Privialged = Privilaged
endmodule

module Violation_Handler (
  input  PCV,
  input  Timeout,
  input  Clock,
  input  [1:0] StepIn,
  output ExceptionFound,
  output [1:0] StepOut,
  output ExceptionCleared,
  output [15:0] ExceptionAddress
);

  wire or_1_out;
  wire [15:0] multiplexer_1_out, multiplexer_2_out, multiplexer_3_out, multiplexer_4_out;

  Multiplexer #(.width(16), .enable("false")) multiplexer_1 (
    .in0({16{1'b0}}), .in1(16'h8), .out(multiplexer_1_out), .sel(Timeout));
  Multiplexer #(.width(16), .enable("false")) multiplexer_2 (
    .in0(16'h2), .in1(16'ha), .out(multiplexer_2_out), .sel(Timeout));
  Multiplexer #(.width(16), .enable("false")) multiplexer_3 (
    .in0(16'h4), .in1(16'hc), .out(multiplexer_3_out), .sel(Timeout));
  Multiplexer #(.width(16), .enable("false")) multiplexer_4 (
    .in0(16'h6), .in1(16'he), .out(multiplexer_4_out), .sel(Timeout));
  Multiplexer #(.select(2), .width(16), .enable("false")) multiplexer_5 (
    .in0(multiplexer_1_out), .in1(multiplexer_2_out), .in2(multiplexer_3_out), .in3(multiplexer_4_out),
    .out(ExceptionAddress), .sel(StepIn));
  and and_1 (ExceptionCleared, 1'b0, 1'b0);
  or or_1 (or_1_out, PCV, Timeout);
  and and_2 (ExceptionFound, or_1_out, ~ExceptionCleared);  // AND_Gate

  assign StepOut = 2'b00;

  // Other names for the same wires on the sheet: StepOut_t = ExceptionCleared
endmodule
